// Digital circuit shift-add-multiplier.dig as structural Verilog
// RAM-backed iterative 8x8 multiplier. High byte=multiplier (control), low byte=multiplicand (data). Shift-and-add into register accumulator, output through tri-state driver.
module shift_add_multiplier (
  input  CLK,
  output [15:0] RESULT
);

  wire BSEL_out;
  wire [2:0] CTR_out;
  wire [15:0] ACC_q, ADD_s, EXTD_out, MUX_out, RAM_d, SHIFT_out;

  RAMSinglePort #(.AddrBits(1), .Bits(16)) RAM (.A(1'b0), .str(1'b0), .C(CLK), .ld(1'b1), .D(RAM_d));
  Counter #(.Bits(3)) CTR (.en(1'b1), .C(CLK), .clr(1'b0), .out(CTR_out));  // open: ovf
  BitSelector #(.Selector_Bits(3)) BSEL (.in(RAM_d[15:8]), .sel(CTR_out), .out(BSEL_out));
  BitExtender #(.Input_Bits(8), .Output_Bits(16)) EXTD (.in(RAM_d[7:0]), .out(EXTD_out));
  BarrelShifter #(.Bits(16), .Direction("left"), .Barrel_Shifter_Mode("logical")) SHIFT (
    .in(EXTD_out), .shift({1'b0, CTR_out}), .out(SHIFT_out));
  Multiplexer #(.Selector_Bits(1), .Bits(16)) MUX (.sel(BSEL_out), .in_0({16{1'b0}}), .in_1(SHIFT_out), .out(MUX_out));
  Add #(.Bits(16)) ADD (.a(MUX_out), .b(ACC_q), .c_i(1'b0), .s(ADD_s));  // open: c_o
  Register #(.Bits(16)) ACC (.D(ADD_s), .C(CLK), .en(1'b1), .Q(ACC_q));
  assign RESULT = 1'b1 ? ACC_q : 16'bz;  // Driver driver_1

  // Notes on the sheet:
  //   contents of RAM (hex, n*v repeats v):
  //   1283
endmodule
