// Digital circuit Address_RW.dig as structural Verilog
module Address_RW (
  input  Ri,
  input  Wi,
  input  [15:0] ADD,
  output R,
  output W
);

  wire ADD_PORT_eq;

  Comparator #(.Bits(16)) ADD_PORT (.a(ADD), .b(16'h1), .eq(ADD_PORT_eq));  // open: gt, lt
  and and_1 (R, Ri, ADD_PORT_eq);
  and and_2 (W, ADD_PORT_eq, Wi);
endmodule

/* Code that sets the parameters or builds the circuit:
address := 0x0000;
*/
