// Digital circuit MCU.dig as structural Verilog
module MCU (
  input  C,
  output PIN1,
  output PIN2,
  output PIN3,
  output PIN4,
  output PIN5,
  output PIN6,
  output PIN7,
  output PIN8,
  output PIN9,
  output PIN10,
  output PIN11,
  output PIN12,
  output PIN13,
  output PIN14,
  output PIN15,
  output PIN16
);

  wire PA0, PA1, PA2, PA3, PA4, PA5, PA6, PA7, PB0, PB1, PB2, PB3, PB4, PB5, PB6, PB7, PWM0_EN, PWM0_out,
       PWM1_EN, PWM1_out, R_IO, R_MM, TC0_in, TC1_in, TC2_in, TC3_in, W_IO, W_MM;
  wire [7:0] undriven_2;
  wire [15:0] undriven;

  mcu_processor mcu_processor_1 (
    .C(C), .DAT(undriven_2), .ADD(undriven), .W_IO(W_IO), .R_IO(R_IO), .W_add(W_MM), .R_add(R_MM));
  TC_periph #(.generic("TC0DATIOadd := 0x0035; TC0DATadd := 0x0036; TC1DATIOadd := 0x0037; TC1DATadd := 0x0038; TC2DATIOadd := 0x0039; TC2DATadd := 0x003A; TC3DATIOadd := 0x0030; TC3DATadd := 0x0031; TCCTRLadd := 0x0032; TCSZIOadd := 0x0033; TCSZadd := 0x0034;")) tc_periph_1 (
    .ADD(undriven), .DAT(undriven_2), .R(R_MM), .IOR(R_IO), .W(W_MM), .IOW(W_IO), .C(C),
    .TCin({TC3_in, TC2_in, TC1_in, TC0_in}));
  PWM #(.generic("PWMCMPadd := 0x0001;")) PWM0 (
    .PWM_out(PWM0_out), .DAT(undriven_2), .ADD(undriven), .R(R_MM), .W(W_MM), .EN(PWM0_EN), .C(C));
  PWM #(.generic("PWMCMPadd := 0x0000;")) PWM2 (
    .PWM_out(PWM1_out), .DAT(undriven_2), .ADD(undriven), .R(R_MM), .W(W_MM), .EN(PWM1_EN), .C(C));
  GPIO_port #(.generic("DDIOAdd := 0x0010; DDMemAdd := 0x0011; PinIOAdd := 0x0012; PinMemAdd := 0x0013; PortIOAdd := 0x0014; PortMemAdd := 0x0015;")) PORTA (
    .ADD(undriven), .DAT(undriven_2), ._0(PA0), ._1(PA1), ._2(PA2), ._3(PA3), ._4(PA4), ._5(PA5), ._6(PA6),
    ._7(PA7), .R(R_MM), .IOR(R_IO), .W(W_MM), .IOW(W_IO), .C(C));
  GPIO_port #(.generic("DDIOAdd := 0x00021; DDMemAdd := 0x0022; PinIOAdd := 0x0023; PinMemAdd := 0x0024; PortIOAdd := 0x0025; PortMemAdd := 0x0026;")) PORTB (
    .ADD(undriven), .DAT(undriven_2), ._0(PB0), ._1(PB1), ._2(PB2), ._3(PB3), ._4(PB4), ._5(PB5), ._6(PB6),
    ._7(PB7), .R(R_MM), .IOR(R_IO), .W(W_MM), .IOW(W_IO), .C(C));
  sysreg #(.generic("regAddress := 0x0030;")) PWMCTRL (
    .ADD(undriven), .DAT(undriven_2), .R(R_MM), .W(W_MM), .C(C), .PWM0_EN(PWM0_EN), .PWM1_EN(PWM1_EN));
  PinMuxGroup #(.generic("pinMuxAddress := 0x1000;")) PIN1_4 (
    .O_0_0(PA0), .O_0_1(PWM0_out), .O_1_0(PA1), .O_1_1(PWM0_out), .O_2_0(PA2), .O_2_1(PWM0_out), .O_3_0(PA3),
    .O_3_1(PWM0_out), .C(C), .ADD(undriven), .DAT(undriven_2), .R_MM(R_MM), .W_MM(W_MM), .P0(PIN1),
    .P1(PIN2), .P2(PIN3), .P3(PIN4), .I_0_0(TC0_in), .I_1_0(TC1_in), .I_2_1(TC2_in), .I_3_1(TC3_in));  // open: I_0_1, I_2_0, I_3_0, I_1_1
  PinMuxGroup #(.generic("pinMuxAddress := 0x1000;")) PIN5_9 (
    .O_0_0(PA4), .O_0_1(PWM1_out), .O_1_0(PA5), .O_1_1(PWM1_out), .O_2_0(PA6), .O_2_1(PWM1_out), .O_3_0(PA7),
    .O_3_1(PWM1_out), .C(C), .ADD(undriven), .DAT(undriven_2), .R_MM(R_MM), .W_MM(W_MM), .P0(PIN5),
    .P1(PIN6), .P2(PIN7), .P3(PIN8), .I_0_0(TC0_in), .I_1_0(TC1_in), .I_2_1(TC2_in), .I_3_1(TC3_in));  // open: I_0_1, I_2_0, I_3_0, I_1_1
  PinMuxGroup #(.generic("pinMuxAddress := 0x1000;")) PIN9_12 (
    .O_0_0(PB0), .O_0_1(PWM0_out), .O_1_0(PB1), .O_1_1(PWM0_out), .O_2_0(PB2), .O_2_1(PWM0_out), .O_3_0(PB3),
    .O_3_1(PWM0_out), .C(C), .ADD(undriven), .DAT(undriven_2), .R_MM(R_MM), .W_MM(W_MM), .P0(PIN9),
    .P1(PIN10), .P2(PIN11), .P3(PIN12), .I_0_0(TC0_in), .I_1_0(TC1_in), .I_2_1(TC2_in), .I_3_1(TC3_in));  // open: I_0_1, I_2_0, I_3_0, I_1_1
  PinMuxGroup #(.generic("pinMuxAddress := 0x1000;")) PIN13_16 (
    .O_0_0(PB4), .O_0_1(PWM1_out), .O_1_0(PB5), .O_1_1(PWM1_out), .O_2_0(PB6), .O_2_1(PWM1_out), .O_3_0(PB7),
    .O_3_1(PWM1_out), .C(C), .ADD(undriven), .DAT(undriven_2), .R_MM(R_MM), .W_MM(W_MM), .P0(PIN13),
    .P1(PIN14), .P2(PIN15), .P3(PIN16), .I_0_0(TC0_in), .I_1_0(TC1_in), .I_2_1(TC2_in), .I_3_1(TC3_in));  // open: I_0_1, I_2_0, I_3_0, I_1_1

  // Other names for the same wires on the sheet: P1 = PIN1; P2 = PIN2; P3 = PIN3; P4 = PIN4; P5 = PIN5; P6 = PIN6;
  //   P7 = PIN7; P8 = PIN8; P9 = PIN9; P10 = PIN10; P11 = PIN11; P12 = PIN12; P13 = PIN13; P14 = PIN14; P15 = PIN15;
  //   P16 = PIN16

  // Notes on the sheet:
  //   Chip Layout
endmodule
