// Digital circuit PinMux.dig as structural Verilog
// Pin multiplexer
// Each physical pin can be connected to 1 or two inputs or outputs. 
// O0: Choice of output for Sel=0
// O1: Choice of output for Sel=1
// I0: Choice of input for Sel = 0
// I1: Choice of input for Sel = 1
// Sel: select the input/output
// DIR: Set direction: 0=output , 1=input.
// NOTE: this signal selects whether the physical pin is in/out, and is seperate from the configuration of a GPIO pin direction
// PIN: ... It's the pin.
module PinMux (
  input  O0,
  input  O1,
  input  Sel,
  input  DIR,
  output PIN,
  output I0,
  output I1
);

  wire driver_2_out, multiplexer_1_out, not_1_out;

  Multiplexer multiplexer_1 (.sel(Sel), .in_0(O0), .in_1(O1), .out(multiplexer_1_out));
  assign PIN = DIR ? multiplexer_1_out : 1'bz;  // Driver driver_1
  not not_1 (not_1_out, DIR);
  assign driver_2_out = not_1_out ? PIN : 1'bz;  // Driver driver_2
  Demultiplexer demultiplexer_1 (.sel(Sel), .in(driver_2_out), .out_0(I0), .out_1(I1));
endmodule
