// Digital circuit PinMuxGroup.dig as structural Verilog
module PinMuxGroup (
  input  O_0_0,
  input  O_0_1,
  input  O_1_0,
  input  O_1_1,
  input  O_2_0,
  input  O_2_1,
  input  O_3_0,
  input  O_3_1,
  input  C,
  input  [15:0] ADD,
  input  [7:0] DAT,
  input  R_MM,
  input  W_MM,
  output P0,
  output P1,
  output P2,
  output P3,
  output I_0_0,
  output I_0_1,
  output I_1_0,
  output I_2_0,
  output I_2_1,
  output I_3_0,
  output I_3_1,
  output I_1_1
);

  wire address_rw_1_w, DIR0, DIR1, DIR2, DIR3, SEL0, SEL1, SEL2, SEL3;

  Address_RW #(.generic("address := args.pinMuxAddress;")) address_rw_1 (
    .Ri(R_MM), .Wi(W_MM), .ADD(ADD), .W(address_rw_1_w));  // open: R
  Register #(.Bits(8)) register_1 (
    .D(DAT), .C(C), .en(address_rw_1_w), .Q({SEL3, DIR3, SEL2, DIR2, SEL1, DIR1, SEL0, DIR0}));
  PinMux pinmux_1 (.PIN(P0), .I0(I_0_0), .I1(I_0_1), .O0(O_0_0), .O1(O_0_1), .DIR(DIR0), .Sel(SEL0));
  PinMux pinmux_2 (.PIN(P1), .I0(I_1_0), .I1(I_1_1), .O0(O_1_0), .O1(O_1_1), .DIR(DIR1), .Sel(SEL1));
  PinMux pinmux_3 (.PIN(P2), .I0(I_2_0), .I1(I_2_1), .O0(O_2_0), .O1(O_2_1), .DIR(DIR2), .Sel(SEL2));
  PinMux pinmux_4 (.PIN(P3), .I0(I_3_0), .I1(I_3_1), .O0(O_3_0), .O1(O_3_1), .DIR(DIR3), .Sel(SEL3));

  // Other names for the same wires on the sheet: I_00 = I_0_0; I_01 = I_0_1; I_10 = I_1_0; I_11 = I_1_1; I_20 = I_2_0;
  //   I_21 = I_2_1; I_30 = I_3_0; I_31 = I_3_1; O_00 = O_0_0; O_01 = O_0_1; O_10 = O_1_0; O_11 = O_1_1; O_20 = O_2_0;
  //   O_21 = O_2_1; O_30 = O_3_0; O_31 = O_3_1
endmodule

/* Code that sets the parameters or builds the circuit:
pinMuxAddress := 0x0000;
*/
