// Digital circuit Full Adder.dig as structural Verilog
module Full_Adder (
  input  Ci,
  input  A,
  input  B,
  output OUT,
  output Co
);

  wire and_1_out, and_2_out, xor_1_out;

  xor xor_1 (xor_1_out, A, B);
  and and_1 (and_1_out, xor_1_out, Ci);
  and and_2 (and_2_out, B, A);
  xor xor_2 (OUT, Ci, xor_1_out);
  or or_1 (Co, and_1_out, and_2_out);
endmodule

/* Test case:
A B Ci  OUT Co
0 0 0  0 0
0 0 1  1 0
0 1 0  1 0
0 1 1  0 1
1 0 0  1 0
1 0 1  0 1
1 1 0  0 1
1 1 1  1 1
*/
