// Digital circuit control.dig as structural Verilog
module control (
  input  Z,
  input  N,
  input  C,
  input  [15:0] INSTR,
  output NXT_add,
  output ALU_data,
  output R_add,
  output SRC_data,
  output ALU_ADR,
  output ALU_BRI,
  output [4:0] OP_ALU,
  output [7:0] ImmVal,
  output W_add,
  output W_reg,
  output j_abs,
  output j_rel,
  output skip,
  output Imm_data,
  output Imm_add,
  output [11:0] rjmp,
  output rjmp_add,
  output [3:0] reg_src,
  output [3:0] reg_dest,
  output Ra_add,
  output R_a,
  output R_IO,
  output W_IO
);

  wire and_1_out, cond, flag_check_1_br, j_rel_t, skip_t;
  wire [31:23] rom_1_d;

  ROM #(.bigEndian("true"), .AddrBits(8), .Bits(32)) rom_1 (
    .A(INSTR[15:8]), .sel(1'b1),
    .D({rom_1_d, R_IO, W_IO, cond, rjmp_add, Imm_add, Imm_data, skip_t, j_rel_t, j_abs, OP_ALU, W_reg, W_add, ALU_BRI, ALU_ADR, Ra_add, R_add, SRC_data, ALU_data, NXT_add}));
  flag_check flag_check_1 (.Co(C), .N(N), .Z(Z), .s(INSTR[6:4]), .br(flag_check_1_br));
  and and_1 (and_1_out, flag_check_1_br, j_rel_t);
  Multiplexer multiplexer_1 (.sel(cond), .in_0(j_rel_t), .in_1(and_1_out), .out(j_rel));
  or or_1 (skip, skip_t, j_rel);

  assign ImmVal = {INSTR[11:8], INSTR[3:0]};
  assign R_a = INSTR[8];
  assign reg_dest = INSTR[7:4];
  assign reg_src = INSTR[3:0];
  assign rjmp = INSTR[11:0];

  // Notes on the sheet:
  //   contents of rom_1 (hex, n*v repeats v):
  //   102,302,502,702,922,b22,d22,f22,1102,1302,1502,1722,104,0,0,0
  //   ,2102,2302,0,0,0,2b22,2d22,9*0,16*20100,16*0,16*1142,16*342,16*1342
  //   ,16*2342,118,118,14*0,94,94,15*0,10109,15*0,10085,14*0,16*98000
  //   ,16*148000,14010,14010,14*0,14001
endmodule
