// Digital circuit lsh_l.dig as structural Verilog
module lsh_l (
  input  [7:0] IN,
  input  Ci,
  output [7:0] OUT,
  output Co
);


  assign Co = IN[7];
  assign OUT = {IN[6:0], Ci};
endmodule

/* Test case:
Ci IN  OUT Co
loop(A,128)
  0 (A) (A*2) 0
  1 (A) (A*2 + 1) 0
  0 (A+128) (A*2) 1
  1 (A+128) (A*2+1) 1
end loop
*/
