// Digital circuit rsh_a.dig as structural Verilog
module rsh_a (
  input  [7:0] IN,
  output [7:0] OUT,
  output Co
);


  assign Co = IN[0];
  assign OUT = {{2{IN[7]}}, IN[6:1]};
endmodule

/* Test case:
IN OUT Co

loop(A,64)
  (A*2) (A) 0
  (A*2+1) (A) 1
end loop

loop(A,64)
  (A*2+128) ((A*2+128)/2+128) 0
  (A*2+129) ((A*2+128)/2+128) 1
end loop
*/
