// Digital circuit rsh_l.dig as structural Verilog
module rsh_l (
  input  [7:0] IN,
  input  Ci,
  output [7:0] OUT,
  output Co
);


  assign Co = IN[0];
  assign OUT = {Ci, IN[7:1]};
endmodule

/* Test case:
Ci IN  OUT Co

loop(A,128)
  0 (A*2) (A) 0
  0 (A*2+1) (A) 1
  1 (A*2) (A + 128) 0
  1 (A*2+1) (A + 128) 1
end loop
*/
