// Digital circuit T_latch.dig as structural Verilog
module T_latch (
  input  En,
  input  D,
  output Q,
  output Q_2
);

  wire and_1_out, and_2_out, not_1_out;

  not not_1 (not_1_out, D);
  and and_1 (and_1_out, D, En);
  and and_2 (and_2_out, En, not_1_out);
  nor nor_1 (Q, and_1_out, Q_2);
  nor nor_2 (Q_2, Q, and_2_out);
endmodule
