// Digital circuit all-components.dig as structural Verilog
module all_components (
  input  In,
  input  Clock,
  output Out
);

  wire Function_p2, notconnected_1_out, ProgramMemory_p1, PullUp_out, scope_1_p2, sevenseg_1_p1;

  // And And is placed but not wired
  DipSwitch DipSwitch ();  // open: out
  // StepperMotorUnipolar StepperMotorUnipolar: pin names not known; wires that end beside it: 1'b1
  Counter Counter ();  // open: en, C, clr, out, ovf
  // ProgramMemory ProgramMemory: pin names not known; wires that end beside it: ProgramMemory_p1
  Div Div ();  // open: a, b, q, r
  BitSelector BitSelector ();  // open: in, sel, out
  Switch Switch ();  // open: A, B
  // Or Or is placed but not wired
  // Probe Probe on scope_1_p2
  PowerSupply PowerSupply ();  // open: VDD, GND
  CounterPreset CounterPreset ();  // open: en, C, dir, in, ld, clr, out, ovf
  RAMSinglePort RAMSinglePort ();  // open: A, str, C, ld, D
  Comparator Comparator ();  // open: a, b, gt, eq, lt
  PriorityEncoder PriorityEncoder ();  // open: in0, in1, num, any
  Reset Reset ();  // open: out
  // SwitchDT SwitchDT: pin names not known
  // Not Not is placed but not wired
  // Scope #(.label("Scope")) scope_1: pin names not known; wires that end beside it: 1'b0, scope_1_p2, 1'b1
  D_FF D_FF ();  // open: D, C, Q, nQ
  Register Register ();  // open: D, C, en, Q
  RAMSinglePortSel RAMSinglePortSel ();  // open: A, CS, WE, OE, D
  Neg #(.label("Neg")) neg_1 ();  // open: in, out
  // Relay Relay: pin names not known
  // PlainSwitch PlainSwitch: pin names not known
  LedMatrix LedMatrix ();  // open: rows, column
  // NAnd NAnd is placed but not wired
  // NotConnected on notconnected_1_out
  // ScopeTrigger #(.label("ScopeTrigger")) scopetrigger_1: pin names not known; wires that end beside it: notconnected_1_out
  D_FF_AS D_FF_AS ();  // open: Set, D, C, Clr, Q, nQ
  RegisterFile RegisterFile ();  // open: Din, we, Rw, C, Ra, Rb, Da, Db
  RAMDualPort RAMDualPort ();  // open: A, Din, str, C, ld, D
  BitExtender BitExtender ();  // open: in, out
  BusSplitter #(.label("BusSplitter")) bussplitter_1 ();  // open: D, OE, D0
  // RelayDT RelayDT: pin names not known
  // PlainSwitchDT PlainSwitchDT: pin names not known
  VGA VGA ();  // open: R, G, B, H, V, C
  // NOr NOr is placed but not wired
  LED LED (.in(sevenseg_1_p1));
  // SevenSeg #(.label("SevenSeg")) sevenseg_1: pin names not known; wires that end beside it: sevenseg_1_p1
  JK_FF JK_FF ();  // open: J, C, K, Q, nQ
  ROM ROM ();  // open: A, sel, D
  RAMDualAccess RAMDualAccess ();  // open: str, C, ld, A1, Din1, A2, D1, D2
  BarrelShifter BarrelShifter ();  // open: in, shift, out
  Driver #(.label("Driver")) driver_1 ();  // open: in, en, out
  NFET NFET ();  // open: G, D, S
  Diode Diode ();  // open: cathode, anode
  GraphicCard GraphicCard ();  // open: A, str, C, ld, B, D
  // XOr XOr is placed but not wired
  // PolarityAwareLED PolarityAwareLED: pin names not known
  // SevenSegHex #(.label("SevenSegHex")) sevenseghex_1: pin names not known
  JK_FF_AS JK_FF_AS ();  // open: Set, J, C, K, Clr, Q, nQ
  ROMDualPort ROMDualPort ();  // open: A1, s1, A2, s2, D1, D2
  RAMAsync RAMAsync ();  // open: A, D, we, Q
  BitCount #(.label("BitCount")) bitcount_1 ();  // open: in, out
  DriverInvSel #(.label("DriverInvSel")) driverinvsel_1 ();  // open: in, en, out
  PFET PFET ();  // open: G, S, D
  DiodeForward DiodeForward ();  // open: in, out
  Terminal Terminal ();  // open: D, C, en
  // XNOr XNOr is placed but not wired
  LightBulb LightBulb ();  // open: A, B
  SixteenSeg #(.label("SixteenSeg")) sixteenseg_1 ();  // open: led, dp
  RS_FF RS_FF ();  // open: S, C, R, Q, nQ
  EEPROM EEPROM ();  // open: A, CS, WE, OE, D
  BlockRAMDualPort BlockRAMDualPort ();  // open: A, Din, str, C, D
  PRNG PRNG ();  // open: S, se, ne, C, R
  Delay Delay ();  // open: in, out
  FGNFET FGNFET ();  // open: G, D, S
  DiodeBackward DiodeBackward ();  // open: in, out
  Keyboard Keyboard ();  // open: C, en, D, av
  // RGBLED RGBLED: pin names not known; wires that end beside it: In
  // MIDI MIDI: pin names not known
  RS_FF_AS RS_FF_AS ();  // open: S, R, Q, nQ
  EEPROMDualPort EEPROMDualPort ();  // open: A, Din, str, C, ld, D
  Add Add ();  // open: a, b, c_i, s, c_o
  Multiplexer Multiplexer ();  // open: sel, in_0, in_1, out
  Stop Stop ();  // open: stop
  FGPFET FGPFET ();  // open: G, S, D
  PullUp PullUp (.out(PullUp_out));
  // Function Function: pin names not known; wires that end beside it: PullUp_out, Function_p2
  Button Button ();  // open: out
  // RotEncoder RotEncoder: pin names not known; wires that end beside it: Out
  T_FF T_FF ();  // open: T, C, Q, nQ
  LookUpTable LookUpTable ();  // open: in0, in1, out
  Sub Sub ();  // open: a, b, c_i, s, c_o
  Demultiplexer Demultiplexer ();  // open: sel, in, out_0, out_1
  Break Break ();  // open: brk
  TransGate TransGate ();  // open: A, nA, out1, out2
  PullDown PullDown (.out(Function_p2));
  // ButtonLED ButtonLED: pin names not known; wires that end beside it: Clock
  // StepperMotorBipolar StepperMotorBipolar: pin names not known
  Monoflop Monoflop ();  // open: C, R, Q, nQ
  // ProgramCounter ProgramCounter: pin names not known
  Mul Mul ();  // open: a, b, mul
  Decoder Decoder ();  // open: sel, out_0, out_1
  Fuse Fuse ();  // open: A, B

  // Notes on the sheet:
  //   Rectangle
endmodule
