// Digital circuit broken_chain.dig as structural Verilog
module broken_chain (
  input  in_1,
  output out_2
);

  wire pfet_1_d, undriven;

  PFET pfet_1 (.G(in_1), .S(1'b1), .D(pfet_1_d));
  NFET nfet_1 (.G(in_1), .D(pfet_1_d), .S(1'b0));
  PFET pfet_2 (.G(undriven), .S(1'b1), .D(out_2));
  NFET nfet_2 (.G(undriven), .D(out_2), .S(1'b0));
endmodule
