// Digital circuit chained_inverters.dig as structural Verilog
module chained_inverters (
  input  In,
  output Out
);

  wire pfet_1_d;

  PFET pfet_1 (.G(In), .S(1'b1), .D(pfet_1_d));
  NFET nfet_1 (.G(In), .D(pfet_1_d), .S(1'b0));
  PFET pfet_2 (.G(pfet_1_d), .S(1'b1), .D(Out));
  NFET nfet_2 (.G(pfet_1_d), .D(Out), .S(1'b0));
endmodule
