// Digital circuit step1-adder.dig as structural Verilog
module step1_adder (
  input  [7:0] A,
  input  [7:0] B,
  input  Cin,
  output [7:0] S,
  output Cout
);

  Add #(.Bits(8)) ADD (.a(A), .b(B), .c_i(Cin), .s(S), .c_o(Cout));
endmodule
