// Digital circuit ALU_complete.dig as structural Verilog
// 8-bit ALU
// Op-code input  comprises:
// UC Op3 Op2 Op1 Op0 
// Where:
// - Op3-Op0 make a 4-bit select signal to select the arithmetic/logic operation
// - UC is an active-high signal that indicates whether the operation should accept a carry-in
// Instructions that can accept a carry-in have the 0/1 UC bit indicated in the list. If another 
// operation is selected, the UC bit has no effect, and is marked by an X.
// Opcodes:
// UC 0000 	Addition A+B
// UC 0001	Subtraction A-B
// X     0010 	Multiplication A*B lower byte (Carry if higher byte is nonzero)
// X     0011	Multiplication A*B upper byte
// X     0100	Negate A
// UC 0101 	Logical left-shit A
// UC 0110	Logical right-shift A
// X     0111	Arithmetic right-shift A
// X     1000	A AND B
// X     1001	A OR B
// X     1010	A XOR B
// X     1011	NOT A
module ALU_complete (
  input  [7:0] A,
  input  [4:0] Op,
  input  [7:0] B,
  input  Ci,
  output [7:0] Y,
  output Carry,
  output Zero,
  output Neg
);

  wire ADD_co, and_1_out, any_1_out, lsh_l_1_co, pulldown_2_out, rsh_a_1_co, rsh_l_1_co, sub_1_c_o;
  wire [7:0] ADD_out, and_2_out, lsh_l_1_out, neg_1_out, not_1_out, or_1_out, pulldown_1_out, rsh_a_1_out,
       rsh_l_1_out, sub_1_s, xor_1_out;
  wire [15:0] mul_1_mul;

  and and_1 (and_1_out, Op[4], Ci);
  _8bit_adder ADD (.Ci(and_1_out), .IN1(A), .IN2(B), .OUT(ADD_out), .Co(ADD_co));
  lsh_l lsh_l_1 (.IN(A), .Ci(and_1_out), .OUT(lsh_l_1_out), .Co(lsh_l_1_co));
  rsh_l rsh_l_1 (.IN(A), .Ci(and_1_out), .OUT(rsh_l_1_out), .Co(rsh_l_1_co));
  rsh_a rsh_a_1 (.IN(A), .OUT(rsh_a_1_out), .Co(rsh_a_1_co));
  Sub #(.Bits(8)) sub_1 (.a(A), .b(B), .c_i(and_1_out), .s(sub_1_s), .c_o(sub_1_c_o));
  Mul #(.Signed("true"), .Bits(8)) mul_1 (.a(A), .b(B), .mul(mul_1_mul));
  Neg #(.Bits(8)) neg_1 (.in(A), .out(neg_1_out));
  assign and_2_out = A & B;  // And and_2, 8 bits wide
  assign or_1_out = A | B;  // Or or_1, 8 bits wide
  assign xor_1_out = A ^ B;  // XOr xor_1, 8 bits wide
  assign not_1_out = ~A;  // Not not_1, 8 bits wide
  ANY any_1 (.IN(mul_1_mul[15:8]), .OUT(any_1_out));
  PullDown #(.Bits(8)) pulldown_1 (.out(pulldown_1_out));
  PullDown pulldown_2 (.out(pulldown_2_out));
  Multiplexer #(.Selector_Bits(4), .Bits(8)) multiplexer_1 (
    .sel(Op[3:0]), .in_0(ADD_out), .in_1(sub_1_s), .in_2(mul_1_mul[7:0]), .in_3(mul_1_mul[15:8]),
    .in_4(neg_1_out), .in_5(lsh_l_1_out), .in_6(rsh_l_1_out), .in_7(rsh_a_1_out), .in_8(and_2_out),
    .in_9(or_1_out), .in_10(xor_1_out), .in_11(not_1_out), .in_12(pulldown_1_out), .in_13(pulldown_1_out),
    .in_14(pulldown_1_out), .in_15(pulldown_1_out), .out({Neg, Y[6:0]}));
  Multiplexer #(.Selector_Bits(4)) multiplexer_2 (
    .sel(Op[3:0]), .in_0(ADD_co), .in_1(sub_1_c_o), .in_2(any_1_out), .in_3(pulldown_2_out),
    .in_4(pulldown_2_out), .in_5(lsh_l_1_co), .in_6(rsh_l_1_co), .in_7(rsh_a_1_co), .in_8(pulldown_2_out),
    .in_9(pulldown_2_out), .in_10(pulldown_2_out), .in_11(pulldown_2_out), .in_12(pulldown_2_out),
    .in_13(pulldown_2_out), .in_14(pulldown_2_out), .in_15(pulldown_2_out), .out(Carry));
  zero_check zero_check_1 (.IN({Neg, Y[6:0]}), .ZERO(Zero));

  assign Y[7] = Neg;

  // Other names for the same wires on the sheet: Select[3:0] = Op[3:0]; Use_carryin = Op[4]
endmodule
