// Digital circuit ANY.dig as structural Verilog
module ANY (
  input  [7:0] IN,
  output OUT
);

  or or_1 (OUT, IN[0], IN[1], IN[2], IN[3], IN[4], IN[5], IN[6], IN[7]);

  // Notes on the sheet:
  //   IN: Ors all the bits of an 8-bit input
endmodule

/* Test case:
IN  OUT
0  0
loop (A,255)
  (A+1) 1
end loop
*/
