// Digital circuit GPReg_addresses.dig as structural Verilog
// This block contains the 16 processor registers.
// {{de In diesem Block befinden sich die 16 
// Prozessorregister.}}
module GPReg_addresses (
  input  [7:0] WD,
  input  C,
  input  [3:0] src,
  input  [3:0] dest,
  input  WE,
  input  Ra,
  output [7:0] Rdest,
  output [7:0] Rsrc,
  output [15:0] Adr
);

  wire demultiplexer_1_out_0, demultiplexer_1_out_1, demultiplexer_1_out_2, demultiplexer_1_out_3,
       demultiplexer_1_out_4, demultiplexer_1_out_5, demultiplexer_1_out_6, demultiplexer_1_out_7,
       demultiplexer_1_out_8, demultiplexer_1_out_9, demultiplexer_1_out_10, demultiplexer_1_out_11,
       demultiplexer_1_out_12, demultiplexer_1_out_13, demultiplexer_1_out_14, demultiplexer_1_out_15;
  wire [7:0] R0_q, R1_q, R2_q, R3_q, R4_q, R5_q, R6_q, R7_q, R8_q, R9_q, R10_q, R11_q;
  wire [15:0] R12_q, R14_q;

  Demultiplexer #(.Selector_Bits(4)) demultiplexer_1 (
    .sel(dest), .in(WE), .out_0(demultiplexer_1_out_0), .out_1(demultiplexer_1_out_1),
    .out_2(demultiplexer_1_out_2), .out_3(demultiplexer_1_out_3), .out_4(demultiplexer_1_out_4),
    .out_5(demultiplexer_1_out_5), .out_6(demultiplexer_1_out_6), .out_7(demultiplexer_1_out_7),
    .out_8(demultiplexer_1_out_8), .out_9(demultiplexer_1_out_9), .out_10(demultiplexer_1_out_10),
    .out_11(demultiplexer_1_out_11), .out_12(demultiplexer_1_out_12), .out_13(demultiplexer_1_out_13),
    .out_14(demultiplexer_1_out_14), .out_15(demultiplexer_1_out_15));
  Register #(.Bits(8)) R0 (.D(WD), .C(C), .en(demultiplexer_1_out_0), .Q(R0_q));
  Register #(.Bits(8)) R1 (.D(WD), .C(C), .en(demultiplexer_1_out_1), .Q(R1_q));
  Register #(.Bits(8)) R2 (.D(WD), .C(C), .en(demultiplexer_1_out_2), .Q(R2_q));
  Register #(.Bits(8)) R3 (.D(WD), .C(C), .en(demultiplexer_1_out_3), .Q(R3_q));
  Register #(.Bits(8)) R4 (.D(WD), .C(C), .en(demultiplexer_1_out_4), .Q(R4_q));
  Register #(.Bits(8)) R5 (.D(WD), .C(C), .en(demultiplexer_1_out_5), .Q(R5_q));
  Register #(.Bits(8)) R6 (.D(WD), .C(C), .en(demultiplexer_1_out_6), .Q(R6_q));
  Register #(.Bits(8)) R7 (.D(WD), .C(C), .en(demultiplexer_1_out_7), .Q(R7_q));
  Register #(.Bits(8)) R8 (.D(WD), .C(C), .en(demultiplexer_1_out_8), .Q(R8_q));
  Register #(.Bits(8)) R9 (.D(WD), .C(C), .en(demultiplexer_1_out_9), .Q(R9_q));
  Register #(.Bits(8)) R10 (.D(WD), .C(C), .en(demultiplexer_1_out_10), .Q(R10_q));
  Register #(.Bits(8)) R11 (.D(WD), .C(C), .en(demultiplexer_1_out_11), .Q(R11_q));
  Register #(.Bits(8)) R12 (.D(WD), .C(C), .en(demultiplexer_1_out_12), .Q(R12_q[15:8]));
  Register #(.Bits(8)) R13 (.D(WD), .C(C), .en(demultiplexer_1_out_13), .Q(R12_q[7:0]));
  Register #(.Bits(8)) R14 (.D(WD), .C(C), .en(demultiplexer_1_out_14), .Q(R14_q[15:8]));
  Register #(.Bits(8)) R15 (.D(WD), .C(C), .en(demultiplexer_1_out_15), .Q(R14_q[7:0]));
  Multiplexer #(.Selector_Bits(4), .Bits(8)) multiplexer_1 (
    .sel(dest), .in_0(R0_q), .in_1(R1_q), .in_2(R2_q), .in_3(R3_q), .in_4(R4_q), .in_5(R5_q), .in_6(R6_q),
    .in_7(R7_q), .in_8(R8_q), .in_9(R9_q), .in_10(R10_q), .in_11(R11_q), .in_12(R12_q[15:8]),
    .in_13(R12_q[7:0]), .in_14(R14_q[15:8]), .in_15(R14_q[7:0]), .out(Rdest));
  Multiplexer #(.Selector_Bits(4), .Bits(8)) multiplexer_2 (
    .sel(src), .in_0(R0_q), .in_1(R1_q), .in_2(R2_q), .in_3(R3_q), .in_4(R4_q), .in_5(R5_q), .in_6(R6_q),
    .in_7(R7_q), .in_8(R8_q), .in_9(R9_q), .in_10(R10_q), .in_11(R11_q), .in_12(R12_q[15:8]),
    .in_13(R12_q[7:0]), .in_14(R14_q[15:8]), .in_15(R14_q[7:0]), .out(Rsrc));
  Multiplexer #(.Bits(16)) multiplexer_3 (.sel(Ra), .in_0(R12_q), .in_1(R14_q), .out(Adr));

  // Notes on the sheet:
  //   WD: Data to be stored.
  //   The value applied here is stored when the input WE is set to 1.
  //   src: Number of the source register. 
  //   Defines which register is to be output to Rsrc.
  //   {{de Nummer des Source Registers. Legt fest, welches 
  //   Register an Rsrc ausgegeben werden soll.}}
  //   dest: Number of the destignation register. 
  //   Defines which register is to be output to Rdest. In 
  //   addition, this register will be overwritten if WE is set to 1.
  //   Rdest: Contents of the Destignation Register.
  //   Which register is output is determined by 
  //   the input dest.
  //   Rsrc: Contents of the Source Register.
  //   Which register is output is determined by the input src.
  //   WE: Activate storing. When this input is high, the value at WD is 
  //   stored in the register specified in dest at the next clock signal.
  //   Adr: Address output of pairs R12/R13, R14/R15
endmodule
