// Digital circuit control_checkpoint1.dig as structural Verilog
module control_checkpoint1 (
  input  Z,
  input  N,
  input  C,
  input  [15:0] INSTR,
  output NXT_add,
  output ALU_data,
  output R_add,
  output SRC_data,
  output ALU_ADR,
  output ALU_BRI,
  output [4:0] OP_ALU,
  output [7:0] ImmVal,
  output W_add,
  output W_reg,
  output j_abs,
  output j_rel,
  output skip,
  output Imm_data,
  output Imm_add,
  output [11:0] rjmp,
  output rjmp_add,
  output [3:0] reg_src,
  output [3:0] reg_dest,
  output Ra_add,
  output R_a
);

  ROM #(.bigEndian("true"), .AddrBits(8), .Bits(32)) rom_1 (.A(INSTR[15:8]), .sel(1'b1));  // open: D

  assign ImmVal = {INSTR[11:8], INSTR[3:0]};
  assign R_a = INSTR[8];
  assign reg_dest = INSTR[7:4];
  assign reg_src = INSTR[3:0];
  assign rjmp = INSTR[11:0];

  // Notes on the sheet:
  //   contents of rom_1 (hex, n*v repeats v):
  //   102,302,502,702,922,b22,d22,f22,1102,1302,1502,1722,104,0,0,0
  //   ,2102,2302,0,0,0,2b22,2d22,9*0,16*20100,16*0,16*1142,16*342,16*1342
  //   ,16*2342,118,118,14*0,94,94,15*0,10109,15*0,10085,14*0,16*98000
  //   ,16*148000,14010,14010,14*0,14001
endmodule
