// Digital circuit control_reduced.dig as structural Verilog
module control_reduced (
  input  Z,
  input  N,
  input  C,
  input  [15:0] INSTR,
  output NXT_add,
  output ALU_data,
  output R_add,
  output SRC_data,
  output ALU_ADR,
  output ALU_BRI,
  output [4:0] OP_ALU,
  output [7:0] ImmVal,
  output W_add,
  output W_reg,
  output j_abs,
  output j_rel,
  output skip,
  output Imm_data,
  output Imm_add,
  output [11:0] rjmp,
  output rjmp_add,
  output [3:0] reg_src,
  output [3:0] reg_dest,
  output Ra_add,
  output R_a
);


  assign ImmVal = {INSTR[11:8], INSTR[3:0]};
  assign R_a = INSTR[8];
  assign reg_dest = INSTR[7:4];
  assign reg_src = INSTR[3:0];
  assign rjmp = INSTR[11:0];
endmodule
