// Digital circuit cpu_layout_CHECKPOINT2.dig as structural Verilog
module cpu_layout_CHECKPOINT2 (
  input  in_3,
  input  in_4,
  input  in_5,
  input  in_6,
  input  [3:0] in_7,
  input  [3:0] in_8,
  input  in_9,
  input  [4:0] in_10,
  input  in_11,
  input  in_12,
  input  in_13,
  input  in_14,
  input  in_15,
  input  [7:0] in_20,
  input  clk,
  input  [7:0] DAT_2,
  input  [15:0] ADD_2,
  input  ext_data,
  input  ext_address,
  output [15:0] ADD,
  output [7:0] DAT,
  output [15:0] out_16,
  output out_17,
  output out_18,
  output out_19
);

  wire alu_complete_1_carry, alu_complete_1_neg, alu_complete_1_zero, and_1_out, and_2_out, and_3_out,
       and_4_out, and_5_out, comparator_1_eq;
  wire [7:0] alu_complete_1_y, gpreg_1_rdest, gpreg_1_rsrc, multiplexer_1_out, multiplexer_2_out;
  wire [15:0] pcfinal_1_pc, Program_d;

  assign DAT = ext_data ? DAT_2 : 8'bz;  // Driver driver_1
  assign ADD = ext_address ? ADD_2 : 16'bz;  // Driver driver_2
  pcfinal pcfinal_1 (.abs(in_5), .rel(in_6), .jump(ADD), .C(clk), .PC(pcfinal_1_pc));
  EEPROM #(.AddrBits(16), .isProgramMemory("true"), .Bits(16)) Program (
    .A(pcfinal_1_pc), .CS(1'b1), .WE(1'b0), .OE(1'b1), .D(Program_d));
  Register #(.Bits(16)) IR (.D(Program_d), .C(clk), .en(1'b1), .Q(out_16));
  GPReg gpreg_1 (.WD(DAT), .C(clk), .src(in_7), .dest(in_8), .WE(in_9), .Rdest(gpreg_1_rdest), .Rsrc(gpreg_1_rsrc));
  assign DAT = in_13 ? gpreg_1_rsrc : 8'bz;  // Driver driver_3
  Multiplexer #(.Bits(8)) multiplexer_1 (
    .sel(in_14), .in_0(gpreg_1_rdest), .in_1(gpreg_1_rsrc), .out(multiplexer_1_out));
  Multiplexer #(.Bits(8)) multiplexer_2 (.sel(in_15), .in_0(gpreg_1_rsrc), .in_1(in_20), .out(multiplexer_2_out));
  ALU_complete alu_complete_1 (
    .A(multiplexer_1_out), .Op(in_10), .Y(alu_complete_1_y), .B(multiplexer_2_out), .Ci(out_17),
    .Carry(alu_complete_1_carry), .Zero(alu_complete_1_zero), .Neg(alu_complete_1_neg));
  status_reg status_reg_1 (
    .C(clk), .Zi(alu_complete_1_zero), .Ni(alu_complete_1_neg), .Ci(alu_complete_1_carry), .Zo(out_19),
    .No(out_18), .Co(out_17));
  assign DAT = in_11 ? alu_complete_1_y : 8'bz;  // Driver driver_4
  assign ADD = in_12 ? {{8{1'b0}}, alu_complete_1_y} : 16'bz;  // Driver driver_5
  PullDown #(.Bits(16)) pulldown_1 (.out(ADD));
  and and_1 (and_1_out, ADD[14], ~ADD[15]);  // And
  Comparator comparator_1 (.a(ADD[15]), .b(1'b1), .eq(comparator_1_eq));  // open: gt, lt
  and and_2 (and_2_out, and_1_out, in_4);
  and and_3 (and_3_out, and_1_out, in_3);
  and and_4 (and_4_out, comparator_1_eq, clk, in_4);
  and and_5 (and_5_out, comparator_1_eq, in_3);
  RAMSinglePort #(.AddrBits(14), .Bits(8)) RAM (.A(ADD[13:0]), .str(and_2_out), .C(clk), .ld(and_3_out), .D(DAT));
  EEPROM #(.AddrBits(15), .Bits(8)) FLASH (
    .A(ADD[14:0]), .CS(comparator_1_eq), .WE(and_4_out), .OE(and_5_out), .D(DAT));
  PullDown #(.Bits(8)) pulldown_2 (.out(DAT));

  // Other names for the same wires on the sheet: ALU_add = in_12; ALU_ADR = in_14; ALU_BRI = in_15; ALU_data = in_11;
  //   C = clk; Co = out_17; ImmVal[7:0] = in_20; INSTR[15:0] = out_16; j_abs = in_5; j_rel = in_6; N = out_18;
  //   OP_ALU[4:0] = in_10; R_add = in_3; reg_dest[3:0] = in_8; reg_src[3:0] = in_7; SRC_data = in_13; W_add = in_4;
  //   W_reg = in_9; Z = out_19

  // Notes on the sheet:
  //   Control Circuit
  //   contents of Program (hex, n*v repeats v):
  //   e001a130,f000,a140,f001,a150,f002,a160,f04b,c73,174,d0b4,4061
  //   ,174,d0b1,f000,b,c86,284,138,b160,f002,b130,f003,4073*0,f000,40
  //   contents of FLASH (hex, n*v repeats v):
  //   11,5,14*0,a1,60,1262*0,f
endmodule
