// Digital circuit memconnect.dig as structural Verilog
module memconnect (
  input  clk,
  input  [7:0] Data_Bus,
  input  [15:0] Address_Bus,
  input  write,
  input  read,
  input  ext_data,
  output [7:0] out_6,
  output [15:0] out_7
);

  wire and_1_out, and_2_out, and_3_out, and_4_out, and_5_out, comparator_1_eq;

  assign out_6 = ext_data ? Data_Bus : 8'bz;  // Driver driver_1
  and and_1 (and_1_out, Address_Bus[14], ~Address_Bus[15]);  // And
  Comparator comparator_1 (.a(Address_Bus[15]), .b(1'b1), .eq(comparator_1_eq));  // open: gt, lt
  and and_2 (and_2_out, and_1_out, write);
  and and_3 (and_3_out, and_1_out, read);
  and and_4 (and_4_out, comparator_1_eq, clk, write);
  and and_5 (and_5_out, comparator_1_eq, read);
  RAMSinglePort #(.AddrBits(14), .Bits(8)) RAM (
    .A(Address_Bus[13:0]), .str(and_2_out), .C(clk), .ld(and_3_out), .D(out_6));
  EEPROM #(.AddrBits(15), .Bits(8)) FLASH (
    .A(Address_Bus[14:0]), .CS(comparator_1_eq), .WE(and_4_out), .OE(and_5_out), .D(out_6));

  assign out_7 = Address_Bus;

  // Other names for the same wires on the sheet: C = clk; mem2data = read; str_mem = write

  // Notes on the sheet:
  //   contents of FLASH (hex, n*v repeats v):
  //   11,5,1278*0,f
endmodule
