// Digital circuit 4x8bitreg_block.dig as structural Verilog
module _4x8bitreg_block (
  input  [7:0] D,
  input  [1:0] A,
  input  W,
  input  C,
  input  R,
  output [7:0] D_O
);

  wire and_1_out, demultiplexer_1_out_0, demultiplexer_1_out_1, demultiplexer_1_out_2, demultiplexer_1_out_3;
  wire [7:0] Address_0_d_o, Address_1_d_o, Address_2_d_o, Address_3_d_o, multiplexer_1_out;

  and and_1 (and_1_out, C, ~W);  // And
  Demultiplexer #(.Selector_Bits(2)) demultiplexer_1 (
    .sel(A), .in(and_1_out), .out_0(demultiplexer_1_out_0), .out_1(demultiplexer_1_out_1),
    .out_2(demultiplexer_1_out_2), .out_3(demultiplexer_1_out_3));
  single_8bit_register Address_0 (.D(D), .W(W), .R(R), .C(demultiplexer_1_out_0), .D_O(Address_0_d_o));
  single_8bit_register Address_1 (.D(D), .W(W), .R(R), .C(demultiplexer_1_out_1), .D_O(Address_1_d_o));
  single_8bit_register Address_2 (.D(D), .W(W), .R(R), .C(demultiplexer_1_out_2), .D_O(Address_2_d_o));
  single_8bit_register Address_3 (.D(D), .W(W), .R(R), .C(demultiplexer_1_out_3), .D_O(Address_3_d_o));
  // Probe Reg 0 on Address_0_d_o
  // Probe Reg 1 on Address_1_d_o
  // Probe Reg 2 on Address_2_d_o
  // Probe Reg 3 on Address_3_d_o
  Multiplexer #(.Selector_Bits(2), .Bits(8)) multiplexer_1 (
    .sel(A), .in_0(Address_0_d_o), .in_1(Address_1_d_o), .in_2(Address_2_d_o), .in_3(Address_3_d_o),
    .out(multiplexer_1_out));
  assign D_O = R ? multiplexer_1_out : 8'bz;  // Driver driver_1
  PullDown #(.Bits(8)) pulldown_1 (.out(D_O));
endmodule

/* Test case:
C A D !W R  D_O

loop (B, 4)
  

    0 (B) 0 0 0   0
    C (B) 0 0 0   0
    C (B) X 1 1   0
    C (B) X 1 1   0
    C (B) 0 0 1   0

    loop (E, 256)
      C (B) (E)  0 0  0
      C (B)  X   1 1 (E)
    end loop
end loop
*/
