// Digital circuit 4x_8bit_register_full.dig as structural Verilog
// Single 8-bit register. D_O port has an internal buffer so should be connectable to the input bus.
module _4x_8bit_register_full (
  input  [7:0] D,
  input  C,
  input  R,
  input  A0,
  input  A1,
  input  W,
  output [7:0] D_O
);

  wire and_1_out, and_2_out, and_3_out, and_4_out, and_5_out, and_6_out, and_7_out, and_8_out, and_9_out,
       and_10_out, and_11_out, and_12_out, driver_1_out, driver_2_out, driver_3_out, driver_4_out;
  wire [0:0] d_ms_21_p3, d_ms_22_p3, d_ms_23_p3, d_ms_24_p3, d_ms_25_p3, d_ms_26_p3, d_ms_27_p3, d_ms_28_p3,
       d_ms_29_p3, d_ms_30_p3, d_ms_31_p3, d_ms_32_p3;
  wire [4:0] d_ms_1_p3, d_ms_2_p3, d_ms_3_p3, d_ms_4_p3;

  and and_1 (and_1_out, A1, A0);
  and and_2 (and_2_out, ~A1, A0);  // And
  and and_3 (and_3_out, A1, ~A0);  // And
  and and_4 (and_4_out, ~A1, ~A0);  // And
  and and_5 (and_5_out, and_1_out, ~W);  // And
  and and_6 (and_6_out, and_1_out, R);
  and and_7 (and_7_out, and_2_out, ~W);  // And
  and and_8 (and_8_out, and_2_out, R);
  and and_9 (and_9_out, and_3_out, ~W);  // And
  and and_10 (and_10_out, and_3_out, R);
  and and_11 (and_11_out, and_4_out, ~W);  // And
  and and_12 (and_12_out, and_4_out, R);
  assign driver_1_out = and_5_out ? C : 1'bz;  // Driver driver_1
  assign driver_2_out = and_7_out ? C : 1'bz;  // Driver driver_2
  assign driver_3_out = and_9_out ? C : 1'bz;  // Driver driver_3
  assign driver_4_out = and_11_out ? C : 1'bz;  // Driver driver_4
  // D_MS d_ms_1: pin names not known; wires that end beside it: D[7], driver_1_out, d_ms_1_p3[4]
  // D_MS d_ms_2: pin names not known; wires that end beside it: D[7], driver_2_out, d_ms_2_p3[4]
  // D_MS d_ms_3: pin names not known; wires that end beside it: D[7], driver_3_out, d_ms_3_p3[4]
  // D_MS d_ms_4: pin names not known; wires that end beside it: D[7], driver_4_out, d_ms_4_p3[4]
  // D_MS d_ms_5: pin names not known; wires that end beside it: D[6], driver_1_out, d_ms_1_p3[3]
  // D_MS d_ms_6: pin names not known; wires that end beside it: D[6], driver_2_out, d_ms_2_p3[3]
  // D_MS d_ms_7: pin names not known; wires that end beside it: D[6], driver_3_out, d_ms_3_p3[3]
  // D_MS d_ms_8: pin names not known; wires that end beside it: D[6], driver_4_out, d_ms_4_p3[3]
  // D_MS d_ms_9: pin names not known; wires that end beside it: D[5], driver_1_out, d_ms_1_p3[2]
  // D_MS d_ms_10: pin names not known; wires that end beside it: D[5], driver_2_out, d_ms_2_p3[2]
  // D_MS d_ms_11: pin names not known; wires that end beside it: D[5], driver_3_out, d_ms_3_p3[2]
  // D_MS d_ms_12: pin names not known; wires that end beside it: D[5], driver_4_out, d_ms_4_p3[2]
  // D_MS d_ms_13: pin names not known; wires that end beside it: D[4], driver_1_out, d_ms_1_p3[1]
  // D_MS d_ms_14: pin names not known; wires that end beside it: D[4], driver_2_out, d_ms_2_p3[1]
  // D_MS d_ms_15: pin names not known; wires that end beside it: D[4], driver_3_out, d_ms_3_p3[1]
  // D_MS d_ms_16: pin names not known; wires that end beside it: D[4], driver_4_out, d_ms_4_p3[1]
  // D_MS d_ms_17: pin names not known; wires that end beside it: D[3], driver_1_out, d_ms_1_p3[0]
  // D_MS d_ms_18: pin names not known; wires that end beside it: D[3], driver_2_out, d_ms_2_p3[0]
  // D_MS d_ms_19: pin names not known; wires that end beside it: D[3], driver_3_out, d_ms_3_p3[0]
  // D_MS d_ms_20: pin names not known; wires that end beside it: D[3], driver_4_out, d_ms_4_p3[0]
  // D_MS d_ms_21: pin names not known; wires that end beside it: D[2], driver_1_out, d_ms_21_p3[0]
  // D_MS d_ms_22: pin names not known; wires that end beside it: D[2], driver_2_out, d_ms_22_p3[0]
  // D_MS d_ms_23: pin names not known; wires that end beside it: D[2], driver_3_out, d_ms_23_p3[0]
  // D_MS d_ms_24: pin names not known; wires that end beside it: D[2], driver_4_out, d_ms_24_p3[0]
  // D_MS d_ms_25: pin names not known; wires that end beside it: D[1], driver_1_out, d_ms_25_p3[0]
  // D_MS d_ms_26: pin names not known; wires that end beside it: D[1], driver_2_out, d_ms_26_p3[0]
  // D_MS d_ms_27: pin names not known; wires that end beside it: D[1], driver_3_out, d_ms_27_p3[0]
  // D_MS d_ms_28: pin names not known; wires that end beside it: D[1], driver_4_out, d_ms_28_p3[0]
  // D_MS d_ms_29: pin names not known; wires that end beside it: D[0], driver_1_out, d_ms_29_p3[0]
  PullDown pulldown_1 (.out(driver_1_out));
  // D_MS d_ms_30: pin names not known; wires that end beside it: D[0], driver_2_out, d_ms_30_p3[0]
  PullDown pulldown_2 (.out(driver_2_out));
  // D_MS d_ms_31: pin names not known; wires that end beside it: D[0], driver_3_out, d_ms_31_p3[0]
  PullDown pulldown_3 (.out(driver_3_out));
  // D_MS d_ms_32: pin names not known; wires that end beside it: D[0], driver_4_out, d_ms_32_p3[0]
  PullDown pulldown_4 (.out(driver_4_out));
  assign D_O = and_6_out ? {d_ms_1_p3, d_ms_21_p3[0], d_ms_25_p3[0], d_ms_29_p3[0]} : 8'bz;  // Driver driver_5
  assign D_O = and_8_out ? {d_ms_2_p3, d_ms_22_p3[0], d_ms_26_p3[0], d_ms_30_p3[0]} : 8'bz;  // Driver driver_6
  assign D_O = and_10_out ? {d_ms_3_p3, d_ms_23_p3[0], d_ms_27_p3[0], d_ms_31_p3[0]} : 8'bz;  // Driver driver_7
  assign D_O = and_12_out ? {d_ms_4_p3, d_ms_24_p3[0], d_ms_28_p3[0], d_ms_32_p3[0]} : 8'bz;  // Driver driver_8
  PullDown #(.Bits(8)) pulldown_5 (.out(D_O));

  // Notes on the sheet:
  //   R: 1 = Read
  //   W: 0 = Write, default 1
endmodule

/* Test case:
C A0 A1 D !W R  D_O

loop (B, 2)
  loop (D, 2)

    0 (B) (D) 0 0 0   0
    C (B) (D) 0 0 0   0
    C (B) (D) X 1 1   0
    C (B) (D) X 1 1   0
    C (B) (D) 0 0 1   0

    loop (A, 256)
      C (B) (D) (A)  0 0  0
      C (B) (D)  X   1 1 (A)
    end loop
  end loop
end loop
*/
