// Digital circuit 8x8bitreg_block.dig as structural Verilog
module _8x8bitreg_block (
  input  [7:0] D,
  input  [2:0] A,
  input  W,
  input  C,
  input  R,
  output [7:0] D_O
);

  wire and_1_out, and_2_out, or_1_out, or_2_out;
  wire [7:0] Address_0_3__green_d_o, Address_4_7__blue_d_o, multiplexer_1_out;

  or or_1 (or_1_out, W, A[2]);
  and and_1 (and_1_out, R, ~A[2]);  // And
  or or_2 (or_2_out, W, ~A[2]);  // Or
  and and_2 (and_2_out, R, A[2]);
  _4x8bitreg_block Address_0_3__green (
    .D(D), .A(A[1:0]), .W(or_1_out), .C(C), .R(and_1_out), .D_O(Address_0_3__green_d_o));
  _4x8bitreg_block Address_4_7__blue (
    .D(D), .A(A[1:0]), .W(or_2_out), .C(C), .R(and_2_out), .D_O(Address_4_7__blue_d_o));
  Multiplexer #(.Bits(8)) multiplexer_1 (
    .sel(A[2]), .in_0(Address_0_3__green_d_o), .in_1(Address_4_7__blue_d_o), .out(multiplexer_1_out));
  assign D_O = R ? multiplexer_1_out : 8'bz;  // Driver driver_1
  PullDown #(.Bits(8)) pulldown_1 (.out(D_O));

  // Notes on the sheet:
  //   W: default 1
endmodule

/* Test case:
C A D !W R  D_O

loop (B, 8)
  

    0 (B) 0 0 0   0
    C (B) 0 0 0   0
    C (B) X 1 1   0
    C (B) X 1 1   0
    C (B) 0 0 1   0

    loop (E, 256)
      C (B) (E)  0 0  0
      C (B)  X   1 1 (E)
    end loop
end loop
*/
