// Digital circuit pcfinal.dig as structural Verilog
// Program Counter for 10-bit program memory
// Incorporates a program counter register and branching logic.
// Inputs:
// C	Clock
// R	Reset register to 0
// jump[10]	Increment or absolute address to branch to
// rel	PC is incremented by jump if rel is high
// abs	PC is loaded with jump if abs is high (if rel and abs are high, abs wins)
// Outputs:
// PC[10]	Current instruction address
// NEXT[10]	PC + 1 (next address if no branch)
module pcfinal (
  input  abs,
  input  rel,
  input  [15:0] jump,
  input  C,
  output [15:0] PC
);

  wire [15:0] ADD_1_s, ADD_JUMP_s, multiplexer_1_out, multiplexer_2_out;

  Register #(.Bits(16), .isProgramCounter("true")) u_PC (.D(multiplexer_2_out), .C(C), .en(1'b1), .Q(PC));
  Add #(.Bits(16)) ADD_1 (.a(PC), .b(16'h1), .c_i(1'b0), .s(ADD_1_s));  // open: c_o
  Add #(.Bits(16)) ADD_JUMP (.a(PC), .b(jump), .c_i(1'b0), .s(ADD_JUMP_s));  // open: c_o
  Multiplexer #(.Bits(16)) multiplexer_1 (.sel(rel), .in_0(ADD_1_s), .in_1(ADD_JUMP_s), .out(multiplexer_1_out));
  Multiplexer #(.Bits(16)) multiplexer_2 (.sel(abs), .in_0(multiplexer_1_out), .in_1(jump), .out(multiplexer_2_out));
endmodule
