// Digital circuit step-3-register-file-goal.dig as structural Verilog
module step_3_register_file_goal (
  input  [7:0] Din,
  input  [1:0] Rw,
  input  WE,
  input  CLK,
  input  [1:0] Ra,
  input  [1:0] Rb,
  output [7:0] Da,
  output [7:0] Db
);

  wire EN0_out, EN1_out, EN2_out, EN3_out, WDEC_out_0, WDEC_out_1, WDEC_out_2, WDEC_out_3;
  wire [7:0] R0_q, R1_q, R2_q, R3_q;

  Decoder #(.Selector_Bits(2)) WDEC (
    .out_0(WDEC_out_0), .out_1(WDEC_out_1), .out_2(WDEC_out_2), .out_3(WDEC_out_3));  // open: sel
  and EN0 (EN0_out, WDEC_out_0, WE);
  and EN1 (EN1_out, WDEC_out_1, WE);
  and EN2 (EN2_out, WDEC_out_2, WE);
  and EN3 (EN3_out, WDEC_out_3, WE);
  Register #(.Bits(8)) R0 (.D(Din), .C(CLK), .en(EN0_out), .Q(R0_q));
  Register #(.Bits(8)) R1 (.D(Din), .C(CLK), .en(EN1_out), .Q(R1_q));
  Register #(.Bits(8)) R2 (.D(Din), .C(CLK), .en(EN2_out), .Q(R2_q));
  Register #(.Bits(8)) R3 (.D(Din), .C(CLK), .en(EN3_out), .Q(R3_q));
  Multiplexer #(.Selector_Bits(2), .Bits(8)) MUXA (
    .sel(Ra), .in_0(R0_q), .in_1(R1_q), .in_2(R2_q), .in_3(R3_q), .out(Da));
  Multiplexer #(.Selector_Bits(2), .Bits(8)) MUXB (
    .sel(Rb), .in_0(R0_q), .in_1(R1_q), .in_2(R2_q), .in_3(R3_q), .out(Db));
endmodule
