// Digital circuit step-8-pc-program-memory-goal.dig as structural Verilog
module step_8_pc_program_memory_goal (
  input  PC_en,
  input  CLK,
  input  Reset,
  output [7:0] PC_out,
  output [7:0] Instr,
  output PC_ovf
);

  Counter #(.Bits(8)) PC (.en(PC_en), .C(CLK), .clr(Reset), .out(PC_out), .ovf(PC_ovf));
  ROM #(.AddrBits(8), .Bits(8), .isProgramMemory("true")) PROG_MEM (.A(PC_out), .sel(1'b1), .D(Instr));
endmodule
