// Digital circuit 4-1-mux-2-bit-selector-routes-one-of-four-inputs.dig as structural Verilog
module _4_1_mux_2_bit_selector_routes_one_of_four_inputs (
  input  D0,
  input  D1,
  input  D2,
  input  D3,
  input  [1:0] Sel,
  output Y
);

  Multiplexer #(.simulationModel("digital"), .Selector_Bits(2)) M (
    .sel(Sel), .in_0(D0), .in_1(D1), .in_2(D2), .in_3(D3), .out(Y));
endmodule
