// Digital circuit bus-splitter-8-bit-to-4-4-nibbles.dig as structural Verilog
module bus_splitter_8_bit_to_4_4_nibbles (
  input  D,
  output Lo,
  output Hi
);

  BusSplitter bussplitter_1 ();  // open: D, OE, D0
endmodule
