// Digital circuit comparator-to-logic-analog-threshold-drives-digital-gate.dig as structural Verilog
module comparator_to_logic_analog_threshold_drives_digital_gate (
  output Y
);

  wire CMP_p2, POT_p2, Vref_p1, Vs_p2;

  // DcVoltageSource Vs: pin names not known; wires that end beside it: 1'b0, Vs_p2
  // DcVoltageSource Vref: pin names not known; wires that end beside it: Vref_p1
  // Potentiometer POT: pin names not known; wires that end beside it: Vs_p2, POT_p2, 1'b0, POT_p2
  // VoltageComparator #(.outputType("push-pull")) CMP: pin names not known; wires that end beside it: Vref_p1, CMP_p2
  and GA (Y, CMP_p2, 1'b1);
endmodule
