// Digital circuit decoder-2-bit-input-produces-one-hot-outputs.dig as structural Verilog
module decoder_2_bit_input_produces_one_hot_outputs (
  input  [1:0] Sel,
  output Y0,
  output Y1,
  output Y2,
  output Y3
);

  Decoder #(.simulationModel("digital"), .Selector_Bits(2)) DEC (
    .out_0(Y0), .out_1(Y1), .out_2(Y2), .out_3(Y3));  // open: sel
endmodule
