// Digital circuit digital-controlled-analog-switch-in-toggles-analog-path.dig as structural Verilog
module digital_controlled_analog_switch_in_toggles_analog_path (
  input  CTRL
);

  wire R1_p1, Vs_p2;

  // DcVoltageSource Vs: pin names not known; wires that end beside it: 1'b0, Vs_p2
  // SwitchSPST SW1: pin names not known; wires that end beside it: Vs_p2, CTRL
  // Resistor R1: pin names not known; wires that end beside it: R1_p1, 1'b0
  // Probe P1 on R1_p1
endmodule
