// Digital circuit digital-gate-driving-analog-load-and-output-drives-resistor.dig as structural Verilog
module digital_gate_driving_analog_load_and_output_drives_resistor (
  input  A,
  input  B
);

  wire G1_out;

  and G1 (G1_out, A, B);
  // Resistor R1: pin names not known; wires that end beside it: G1_out, 1'b0
  // Probe P1 on G1_out
endmodule
