// Digital circuit digital-servo-loop-dac-to-opamp-to-adc-feedforward.dig as structural Verilog
module digital_servo_loop_dac_to_opamp_to_adc_feedforward (
  input  CLK,
  output Q0,
  output Q1,
  output Q2,
  output Q3
);

  wire Vref_p2;

  // DcVoltageSource Vref: pin names not known; wires that end beside it: 1'b0, Vref_p2, 1'b1, 1'b0
  // DAC #(.Bits(4)) DAC1: pin names not known; wires that end beside it: 1'b0, 1'b0, Vref_p2, 1'b0
  // OpAmp AMP: pin names not known
  // Resistor Rf: pin names not known
  // DcVoltageSource Vref2: pin names not known; wires that end beside it: Q3
  // Resistor Rin: pin names not known; wires that end beside it: 1'b0, 1'b0
  // ADC #(.Bits(4)) ADC1: pin names not known; wires that end beside it: CLK, Q0, Q1, Q2
endmodule
