// Digital circuit mixed-switching-transient-d_ff-toggles-spdt-with-lrc-load.dig as structural Verilog
module mixed_switching_transient_d_ff_toggles_spdt_with_lrc_load (
  input  CLK
);

  wire FF_nq, FF_q, L1_p2, R1_p1, R2_p2, SW1_p3, Vs_p2;

  // DcVoltageSource Vs: pin names not known; wires that end beside it: 1'b0, Vs_p2
  D_FF #(.simulationModel("digital")) FF (.D(FF_nq), .C(CLK), .Q(FF_q), .nQ(FF_nq));
  // Inductor L1: pin names not known; wires that end beside it: Vs_p2, L1_p2
  // SwitchSPDT SW1: pin names not known; wires that end beside it: L1_p2, FF_q, SW1_p3
  // Resistor R1: pin names not known; wires that end beside it: R1_p1, R1_p1
  // Resistor R2: pin names not known; wires that end beside it: SW1_p3, R2_p2, 1'b0
  // Capacitor C1: pin names not known; wires that end beside it: R2_p2, 1'b0
  // Probe P1 on R1_p1
endmodule
