// Digital circuit priority-encoder-highest-active-input-index.dig as structural Verilog
module priority_encoder_highest_active_input_index (
  input  I0,
  input  I1,
  input  I2,
  input  I3,
  output [1:0] Num,
  output Any
);

  PriorityEncoder #(.Selector_Bits(2)) PE (.in0(I0), .in1(I1), .in2(I2), .in3(I3));  // open: num, any
endmodule
