// Digital circuit ram-write-read-store-and-retrieve-values.dig as structural Verilog
module ram_write_read_store_and_retrieve_values (
  input  [1:0] A,
  input  [7:0] Din,
  input  WE,
  input  C,
  input  LD,
  output [7:0] D
);

  RAMDualPort #(.AddrBits(2)) RAM (.A(A), .Din(Din[0]), .str(WE), .C(C), .ld(LD), .D(D[0]));
  // Pins of 1 and 8 bits meet at Din
  // Pins of 1 and 8 bits meet at D
endmodule
