// Digital circuit register-file-write-and-read-registers.dig as structural Verilog
module register_file_write_and_read_registers (
  input  [7:0] Din,
  input  WE,
  input  [1:0] Rw,
  input  C,
  input  [1:0] Ra,
  input  [1:0] Rb,
  output [7:0] Da,
  output [7:0] Db
);

  RegisterFile RF (.Din(Din[0]), .we(WE), .Rw(Rw), .C(C), .Ra(Ra), .Rb(Rb), .Da(Da[0]), .Db(Db[0]));
  // Pins of 1 and 8 bits meet at Din
  // Pins of 1 and 8 bits meet at Da
  // Pins of 1 and 8 bits meet at Db
endmodule
