// Digital circuit relay-from-digital-logic-and-gate-drives-relay-coil.dig as structural Verilog
module relay_from_digital_logic_and_gate_drives_relay_coil (
  input  A,
  input  B
);

  wire G1_out, R1_p1, Vs_p2;

  and G1 (G1_out, A, B);
  // DcVoltageSource Vs: pin names not known; wires that end beside it: 1'b0, Vs_p2
  // Relay #(.simulationModel("digital")) RLY: pin names not known; wires that end beside it: G1_out, Vs_p2
  // Resistor R1: pin names not known; wires that end beside it: R1_p1, 1'b0
  // Probe P1 on R1_p1
endmodule
