// Digital circuit rom-lookup-read-preloaded-data-by-address.dig as structural Verilog
module rom_lookup_read_preloaded_data_by_address (
  input  [1:0] A,
  output [7:0] D
);

  ROM #(.AddrBits(2)) ROM (.A(A), .sel(1'b1), .D(D[0]));
  // Pins of 1 and 8 bits meet at D

  // Notes on the sheet:
  //   contents of ROM (hex, n*v repeats v):
  //   1
endmodule
