// Digital circuit schmitt-trigger-to-counter-analog-sine-drives-digital-count.dig as structural Verilog
module schmitt_trigger_to_counter_analog_sine_drives_digital_count (
  output [3:0] Q
);

  wire R1_p2, Vs_p1;

  // AcVoltageSource Vs: pin names not known; wires that end beside it: Vs_p1, 1'b0
  // Resistor R1: pin names not known; wires that end beside it: Vs_p1, R1_p2
  // SchmittInverting SCH: pin names not known; wires that end beside it: R1_p2, 1'b1
  Counter #(.simulationModel("digital")) CNT (.en(1'b1), .C(1'b1), .out(Q[0]));  // open: clr, ovf
  // Pins of 1 and 4 bits meet at Q
endmodule
