// Digital circuit sr-latch-from-nand-gates-set-hold-reset.dig as structural Verilog
module sr_latch_from_nand_gates_set_hold_reset (
  input  nS,
  input  nR,
  output Q
);

  // NAnd N1 is placed but not wired
  // NAnd N2 is placed but not wired
endmodule
