// Digital circuit test-rc-analog-ui.dig as structural Verilog
module test_rc_analog_ui (
);

  wire R1_p2, Vs_p1;

  // AcVoltageSource #(.Amplitude(5), .Frequency(100)) Vs: pin names not known; wires that end beside it: Vs_p1, 1'b0
  // Resistor #(.resistance(1000)) R1: pin names not known; wires that end beside it: Vs_p1, R1_p2
  // Capacitor #(.capacitance("1.0E-6")) C1: pin names not known; wires that end beside it: R1_p2, 1'b0
endmodule
