// Digital circuit t-flip-flop-ripple-counter-review.dig as structural Verilog
module t_flip_flop_ripple_counter_review (
  input  CLK,
  output Q0,
  output Q1,
  output Q2,
  output Q3
);

  wire A2_out, A3_out;

  and A2 (A2_out, Q0, Q1);
  and A3 (A3_out, Q0, Q1, Q2);
  T_FF T1 (.T(1'b1), .C(CLK), .Q(Q0));  // open: nQ
  T_FF T2 (.T(Q0), .C(CLK), .Q(Q1));  // open: nQ
  T_FF T3 (.T(A2_out), .C(CLK), .Q(Q2));  // open: nQ
  T_FF T4 (.T(A3_out), .C(CLK), .Q(Q3));  // open: nQ
endmodule
