// Digital circuit Dual_Address_RW.dig as structural Verilog
module Dual_Address_RW (
  input  R0,
  input  W0,
  input  R1,
  input  W1,
  input  [15:0] ADD,
  output R,
  output W
);

  wire ADD_PORT_2_eq, ADD_PORT_eq, and_1_out, and_2_out, and_3_out, and_4_out;

  Comparator #(.Bits(16)) ADD_PORT (.a(ADD), .b(16'h1), .eq(ADD_PORT_eq));  // open: gt, lt
  Comparator #(.Bits(16)) ADD_PORT_2 (.a(ADD), .b(16'h1), .eq(ADD_PORT_2_eq));  // open: gt, lt
  and and_1 (and_1_out, R0, ADD_PORT_eq);
  and and_2 (and_2_out, ADD_PORT_eq, W0);
  and and_3 (and_3_out, R1, ADD_PORT_2_eq);
  and and_4 (and_4_out, ADD_PORT_2_eq, W1);
  or or_1 (R, and_1_out, and_3_out);
  or or_2 (W, and_2_out, and_4_out);
endmodule

/* Code that sets the parameters or builds the circuit:
address0 := 0x0000;
address1 := 0x0001;
*/
