// Digital circuit GPIO_pin_test.dig as structural Verilog
module GPIO_pin_test (
  input  WDDx,
  input  RDDx,
  input  WPx,
  input  RPx,
  input  WRx,
  input  RRx,
  input  C,
  input  D_2,
  output Pin,
  output D
);

  wire and_1_out, and_2_out, and_3_out, DD_q, multiplexer_1_out, nand_1_out, not_1_out, or_1_out, or_2_out,
       PIN_q, PIN_SYNC_p1, PORT_q, pullup_1_out;

  or or_1 (or_1_out, WRx, WPx, WDDx);
  assign D = or_1_out ? D_2 : 1'bz;  // Driver driver_1
  and and_1 (and_1_out, C, WDDx);
  and and_2 (and_2_out, WPx, D);
  D_FF DD (.D(D), .C(and_1_out), .Q(DD_q));  // open: nQ
  Multiplexer multiplexer_1 (.sel(and_2_out), .in_0(D), .in_1(not_1_out), .out(multiplexer_1_out));
  or or_2 (or_2_out, and_2_out, WRx);
  assign D = RDDx ? DD_q : 1'bz;  // Driver driver_2
  and and_3 (and_3_out, C, or_2_out);
  D_FF PORT (.D(multiplexer_1_out), .C(and_3_out), .Q(PORT_q));  // open: nQ
  assign D = RPx ? PIN_q : 1'bz;  // Driver driver_3
  not not_1 (not_1_out, PORT_q);
  D_FF u_PIN (.D(PIN_SYNC_p1), .C(~C), .Q(PIN_q));  // open: nQ
  assign Pin = DD_q ? PORT_q : 1'bz;  // Driver driver_4
  assign D = RRx ? PORT_q : 1'bz;  // Driver driver_5
  // D_latch PIN_SYNC: pin names not known; wires that end beside it: PIN_SYNC_p1, Pin, C
  nand nand_1 (nand_1_out, ~PORT_q, ~DD_q);  // NAnd
  PullUp pullup_1 (.out(pullup_1_out));
  PFET pfet_1 (.G(nand_1_out), .S(pullup_1_out), .D(Pin));
endmodule
