// Digital circuit GPIO_port.dig as structural Verilog
// GENERIC GPIO port 
// Amend this docs once you've figured out logic - perhaps a truth table for each pin.
// 8 pins.
// Contains three distributed registers. In all registers, the pin number corresponds to the bit position: 
// PORT: Data written to pin or pullup state:
// 	1: high
// 	2: low
// DD: Data direction bit for each pin. Pin number corresponds to bit position.
// 	1: Output
// 	0: Input
// PIN: Value on pin or pullup state. Pin number corresponds to bit position
// 	1: high
// 	0: low
module GPIO_port (
  input  [15:0] ADD,
  input  R,
  input  W,
  input  IOR,
  input  IOW,
  input  C,
  input  [7:0] DAT,
  output _1,
  output _2,
  output _3,
  output _4,
  output _5,
  output _6,
  output _7,
  output _0
);

  wire DAT2GPIO, GPIO2DAT, gpio_pin_1_d, gpio_pin_2_d, gpio_pin_3_d, gpio_pin_4_d, gpio_pin_5_d,
       gpio_pin_6_d, gpio_pin_7_d, gpio_pin_8_d, not_1_out, RDD, RP, RR, WDD, WP, WR;

  Dual_Address_RW #(.generic("address0 := args.PortMemAdd; address1 := args.PortIOAdd;")) PORT_ADD (
    .R0(R), .W0(W), .R1(IOR), .W1(IOW), .ADD(ADD), .R(RR), .W(WR));
  Dual_Address_RW #(.generic("address0 := args.DDMemAdd; address1 := args.DDIOAdd;")) DD_ADD (
    .R0(R), .W0(W), .R1(IOR), .W1(IOW), .ADD(ADD), .R(RDD), .W(WDD));
  Dual_Address_RW #(.generic("address0 := args.PinMemAdd; address1 := args.PinIOAdd;")) PIN_ADD (
    .R0(R), .W0(W), .R1(IOR), .W1(IOW), .ADD(ADD), .R(RP), .W(WP));
  or or_1 (GPIO2DAT, R, IOR);
  or or_2 (DAT2GPIO, W, IOW);
  GPIO_pin gpio_pin_1 (
    .WDDx(WDD), .RDDx(RDD), .WPx(WP), .RPx(RP), .WRx(WR), .RRx(RR), .C(C), .Pin(_0), .D(gpio_pin_1_d));
  GPIO_pin gpio_pin_2 (
    .WDDx(WDD), .RDDx(RDD), .WPx(WP), .RPx(RP), .WRx(WR), .RRx(RR), .C(C), .Pin(_1), .D(gpio_pin_2_d));
  GPIO_pin gpio_pin_3 (
    .WDDx(WDD), .RDDx(RDD), .WPx(WP), .RPx(RP), .WRx(WR), .RRx(RR), .C(C), .Pin(_2), .D(gpio_pin_3_d));
  GPIO_pin gpio_pin_4 (
    .WDDx(WDD), .RDDx(RDD), .WPx(WP), .RPx(RP), .WRx(WR), .RRx(RR), .C(C), .Pin(_3), .D(gpio_pin_4_d));
  GPIO_pin gpio_pin_5 (
    .WDDx(WDD), .RDDx(RDD), .WPx(WP), .RPx(RP), .WRx(WR), .RRx(RR), .C(C), .Pin(_4), .D(gpio_pin_5_d));
  GPIO_pin gpio_pin_6 (
    .WDDx(WDD), .RDDx(RDD), .WPx(WP), .RPx(RP), .WRx(WR), .RRx(RR), .C(C), .Pin(_5), .D(gpio_pin_6_d));
  GPIO_pin gpio_pin_7 (
    .WDDx(WDD), .RDDx(RDD), .WPx(WP), .RPx(RP), .WRx(WR), .RRx(RR), .C(C), .Pin(_6), .D(gpio_pin_7_d));
  GPIO_pin gpio_pin_8 (
    .WDDx(WDD), .RDDx(RDD), .WPx(WP), .RPx(RP), .WRx(WR), .RRx(RR), .C(C), .Pin(_7), .D(gpio_pin_8_d));
  BusSplitter #(.Bits(8)) bussplitter_1 (
    .D(DAT), .OE(not_1_out), .D0(gpio_pin_1_d), .D1(gpio_pin_2_d), .D2(gpio_pin_3_d), .D3(gpio_pin_4_d),
    .D4(gpio_pin_5_d), .D5(gpio_pin_6_d), .D6(gpio_pin_7_d), .D7(gpio_pin_8_d));
  not not_1 (not_1_out, GPIO2DAT);

  // Other names for the same wires on the sheet: ioread = IOR; iowrite = IOW; memread = R; memwrite = W
endmodule

/* Code that sets the parameters or builds the circuit:
DDIOAdd := 0x1000;
DDMemAdd := 0x1003;
PinIOAdd := 0x1006;
PinMemAdd := 0x0010;
PortIOAdd := 0x0013;
PortMemAdd := 0x0016;
*/
