// Digital circuit PWM.dig as structural Verilog
module PWM (
  input  [7:0] DAT,
  input  [15:0] ADD,
  input  W,
  input  R,
  input  EN,
  input  C,
  output PWM_out
);

  wire ADD_PORT_eq, and_1_out, and_2_out, t_ff_1_q, tc_1_int;
  wire [7:0] PWMCMP_q, undriven;

  Comparator #(.Bits(16)) ADD_PORT (.a(ADD), .b(16'h1), .eq(ADD_PORT_eq));  // open: gt, lt
  and and_1 (and_1_out, ADD_PORT_eq, R);
  and and_2 (and_2_out, ADD_PORT_eq, W);
  T_FF t_ff_1 (.T(tc_1_int), .C(~C), .Q(t_ff_1_q));  // open: nQ
  // Probe CNT on undriven
  assign DAT = and_1_out ? PWMCMP_q : 8'bz;  // Driver driver_1
  Register #(.Bits(8)) PWMCMP (.D(DAT), .C(C), .en(and_2_out), .Q(PWMCMP_q));
  TC tc_1 (.DAT(undriven), .DIR(t_ff_1_q), .R(1'b1), .LD(1'b0), .EN(EN), .C(C), .INT(tc_1_int));
  Comparator #(.Bits(8)) comparator_1 (.a(PWMCMP_q), .b(undriven), .lt(PWM_out));  // open: gt, eq

  // Notes on the sheet:
  //   DAT: default 128
  //   ADD: default 128
  //   C: Hz: 100
endmodule

/* Code that sets the parameters or builds the circuit:
PWMCMPadd := 0x3002;
*/
