// Digital circuit 8bit adder.dig as structural Verilog
module _8bit_adder (
  input  Ci,
  input  [7:0] IN2,
  input  [7:0] IN1,
  output [7:0] OUT,
  output Co
);

  wire full_adder_1_co, full_adder_2_co, full_adder_3_co, full_adder_4_co, full_adder_5_co, full_adder_6_co,
       full_adder_7_co;

  Full_Adder full_adder_1 (.Ci(Ci), .A(IN1[0]), .B(IN2[0]), .OUT(OUT[0]), .Co(full_adder_1_co));
  Full_Adder full_adder_2 (.Ci(full_adder_1_co), .A(IN1[1]), .B(IN2[1]), .OUT(OUT[1]), .Co(full_adder_2_co));
  Full_Adder full_adder_3 (.Ci(full_adder_2_co), .A(IN1[2]), .B(IN2[2]), .OUT(OUT[2]), .Co(full_adder_3_co));
  Full_Adder full_adder_4 (.Ci(full_adder_3_co), .A(IN1[3]), .B(IN2[3]), .OUT(OUT[3]), .Co(full_adder_4_co));
  Full_Adder full_adder_5 (.Ci(full_adder_4_co), .A(IN1[4]), .B(IN2[4]), .OUT(OUT[4]), .Co(full_adder_5_co));
  Full_Adder full_adder_6 (.Ci(full_adder_5_co), .A(IN1[5]), .B(IN2[5]), .OUT(OUT[5]), .Co(full_adder_6_co));
  Full_Adder full_adder_7 (.Ci(full_adder_6_co), .A(IN1[6]), .B(IN2[6]), .OUT(OUT[6]), .Co(full_adder_7_co));
  Full_Adder full_adder_8 (.Ci(full_adder_7_co), .A(IN1[7]), .B(IN2[7]), .OUT(OUT[7]), .Co(Co));
endmodule

/* Test case:
Ci IN1 IN2  OUT Co
0 0 0  0 0

loop (A,256)
  loop (B, 256)
    let co1 = ite(((A + B) > 255),1,0);
    let co2 = ite(((A + B + 1) > 255),1,0);
    0 (A) (B)  (A+B) (co1)
    1 (A) (B)  (A+B+1) (co2)
  end loop
end loop
*/
