// Digital circuit mcu_processor.dig as structural Verilog
// ENMT665 Processor.
// Data bus: 8 bits
// Address bus: 16 bits
// ISA available in spreadsheet form in the module files archive.
module mcu_processor (
  input  C,
  input  [7:0] DAT,
  input  [15:0] ADD,
  output R_add,
  output W_add,
  output R_IO,
  output W_IO
);

  wire ALU_ADR, ALU_BRI, alu_complete_1_carry, alu_complete_1_neg, alu_complete_1_zero, ALU_data, and_1_out,
       and_2_out, and_3_out, and_4_out, and_5_out, Co, comparator_1_eq, Imm_add, Imm_data, j_abs, j_rel, N,
       NOP_switch_q, NXT_add, Ra, RA_add, rjmp_add, SKIP, SRC_data, W_reg, Z;
  wire [3:0] reg_dest, reg_src;
  wire [4:0] OP_ALU;
  wire [7:0] alu_complete_1_y, gpreg_addresses_1_rdest, gpreg_addresses_1_rsrc, ImmVal, multiplexer_2_out,
       multiplexer_3_out;
  wire [11:0] rjmp;
  wire [15:0] gpreg_addresses_1_adr, INSTR, IR_q, pcfinal_1_pc, Program_d;

  pcfinal pcfinal_1 (.abs(j_abs), .rel(j_rel), .jump(ADD), .C(C), .PC(pcfinal_1_pc));
  // Probe PC on pcfinal_1_pc
  EEPROM #(.AddrBits(16), .isProgramMemory("true"), .Bits(16)) Program (
    .A(pcfinal_1_pc), .CS(1'b1), .WE(1'b0), .OE(1'b1), .D(Program_d));
  D_FF NOP_switch (.D(SKIP), .C(C), .Q(NOP_switch_q));  // open: nQ
  control control_1 (
    .reg_src(reg_src), .reg_dest(reg_dest), .rjmp(rjmp), .ImmVal(ImmVal), .R_a(Ra), .OP_ALU(OP_ALU),
    .Imm_data(Imm_data), .NXT_add(NXT_add), .ALU_data(ALU_data), .SRC_data(SRC_data), .R_add(R_add),
    .Ra_add(RA_add), .ALU_ADR(ALU_ADR), .ALU_BRI(ALU_BRI), .skip(SKIP), .W_add(W_add), .W_reg(W_reg),
    .rjmp_add(rjmp_add), .Imm_add(Imm_add), .j_abs(j_abs), .j_rel(j_rel), .R_IO(R_IO), .W_IO(W_IO),
    .INSTR(INSTR), .C(Co), .N(N), .Z(Z));
  // Probe Co on Co
  // Probe N on N
  // Probe Z on Z
  assign ADD = NXT_add ? Program_d : 16'bz;  // Driver driver_1
  Register #(.Bits(16)) IR (.D(Program_d), .C(C), .en(1'b1), .Q(IR_q));
  Multiplexer #(.Bits(16)) multiplexer_1 (.sel(NOP_switch_q), .in_0(IR_q), .in_1({16{1'b0}}), .out(INSTR));
  // Probe INSTR on INSTR
  GPReg_addresses gpreg_addresses_1 (
    .WD(DAT), .C(C), .src(reg_src), .dest(reg_dest), .WE(W_reg), .Ra(Ra), .Rdest(gpreg_addresses_1_rdest),
    .Rsrc(gpreg_addresses_1_rsrc), .Adr(gpreg_addresses_1_adr));
  assign ADD = RA_add ? gpreg_addresses_1_adr : 16'bz;  // Driver driver_2
  assign DAT = SRC_data ? gpreg_addresses_1_rsrc : 8'bz;  // Driver driver_3
  Multiplexer #(.Bits(8)) multiplexer_2 (
    .sel(ALU_ADR), .in_0(gpreg_addresses_1_rdest), .in_1(gpreg_addresses_1_rsrc), .out(multiplexer_2_out));
  Multiplexer #(.Bits(8)) multiplexer_3 (
    .sel(ALU_BRI), .in_0(gpreg_addresses_1_rsrc), .in_1(ImmVal), .out(multiplexer_3_out));
  ALU_complete alu_complete_1 (
    .A(multiplexer_2_out), .Op(OP_ALU), .Y(alu_complete_1_y), .B(multiplexer_3_out), .Ci(Co),
    .Carry(alu_complete_1_carry), .Zero(alu_complete_1_zero), .Neg(alu_complete_1_neg));
  // Probe aluop on OP_ALU
  status_reg status_reg_1 (
    .C(C), .Zi(alu_complete_1_zero), .Ni(alu_complete_1_neg), .Ci(alu_complete_1_carry), .Zo(Z), .No(N),
    .Co(Co));
  assign DAT = ALU_data ? alu_complete_1_y : 8'bz;  // Driver driver_4
  assign ADD = rjmp_add ? {{5{rjmp[11]}}, rjmp[10:0]} : 16'bz;  // Driver driver_5
  assign ADD = Imm_add ? {{9{ImmVal[7]}}, ImmVal[6:0]} : 16'bz;  // Driver driver_6
  PullDown #(.Bits(16)) pulldown_1 (.out(ADD));
  and and_1 (and_1_out, ADD[14], ~ADD[15]);  // And
  Comparator comparator_1 (.a(ADD[15]), .b(1'b1), .eq(comparator_1_eq));  // open: gt, lt
  and and_2 (and_2_out, and_1_out, W_add);
  and and_3 (and_3_out, and_1_out, R_add);
  and and_4 (and_4_out, comparator_1_eq, C, W_add);
  and and_5 (and_5_out, comparator_1_eq, R_add);
  RAMSinglePort #(.AddrBits(14), .Bits(8)) RAM (.A(ADD[13:0]), .str(and_2_out), .C(C), .ld(and_3_out), .D(DAT));
  EEPROM #(.AddrBits(15), .Bits(8)) FLASH (
    .A(ADD[14:0]), .CS(comparator_1_eq), .WE(and_4_out), .OE(and_5_out), .D(DAT));
  assign DAT = Imm_data ? ImmVal : 8'bz;  // Driver driver_7
  PullDown #(.Bits(8)) pulldown_2 (.out(DAT));

  // Notes on the sheet:
  //   C: Hz: 5
  //   contents of Program (hex, n*v repeats v):
  //   0,a130,8000,a140,8001,a150,8002,a160,8003,c73,174,d0b4,5f6f,174
  //   ,d0b1,f000,a,c86,284,138,b106,4000,b103,4001
  //   contents of FLASH (hex, n*v repeats v):
  //   11,5,1,1,1276*0,f,9962*0,2b,6164*0,f1,3f,2560*0,fa,8703*0,3,2
endmodule
