// Digital circuit overflow.dig as structural Verilog
module overflow (
  input  [7:0] A,
  input  [7:0] B,
  input  [7:0] S,
  output O
);

  wire and_1_out, nor_1_out;

  and and_1 (and_1_out, A[7], ~S[7], B[7]);  // And
  nor nor_1 (nor_1_out, B[7], ~S[7], A[7]);  // NOr
  or or_1 (O, and_1_out, nor_1_out);
endmodule

/* Test case:
A B S O



loop (J,256)
    loop(K,256)
	let j = signExt(8,J - 128);
	let k = signExt(8,K - 128);
	let sum = signExt(8,j+k);
	let a = ((j)>>7)&1;
	let b = ((k)>>7)&1;
	let s = ((sum)>>7)&1;
	let out = (a&b&(~s)) | ((~a)&(~b)&(s));
	(j) (k) (sum) (out) 	
    end loop
end loop
*/
