// Digital circuit TC.dig as structural Verilog
module TC (
  input  [7:0] DAT,
  input  DIR,
  input  R,
  input  LD,
  input  EN,
  input  C,
  output INT
);

  wire and_1_out, and_2_out, and_3_out, and_4_out, and_5_out, and_6_out, and_7_out, and_8_out, and_9_out,
       and_10_out, and_11_out, and_12_out, and_13_out, and_14_out, and_15_out, and_16_out, and_17_out,
       and_18_out, and_19_out, and_20_out, and_21_out, and_22_out, and_23_out, bussplitter_1_d0,
       bussplitter_1_d1, bussplitter_1_d2, bussplitter_1_d3, bussplitter_1_d4, bussplitter_1_d5,
       bussplitter_1_d6, bussplitter_1_d7, jk_ff_as_1_nq, jk_ff_as_1_q, jk_ff_as_2_nq, jk_ff_as_2_q,
       jk_ff_as_3_nq, jk_ff_as_3_q, jk_ff_as_4_nq, jk_ff_as_4_q, jk_ff_as_5_nq, jk_ff_as_5_q, jk_ff_as_6_nq,
       jk_ff_as_6_q, jk_ff_as_7_nq, jk_ff_as_7_q, jk_ff_as_8_q, multiplexer_1_out, multiplexer_2_out,
       multiplexer_3_out, multiplexer_4_out, multiplexer_5_out, multiplexer_6_out, multiplexer_7_out;

  BusSplitter #(.Bits(8)) bussplitter_1 (
    .D(DAT), .OE(LD), .D0(bussplitter_1_d0), .D1(bussplitter_1_d1), .D2(bussplitter_1_d2),
    .D3(bussplitter_1_d3), .D4(bussplitter_1_d4), .D5(bussplitter_1_d5), .D6(bussplitter_1_d6),
    .D7(bussplitter_1_d7));
  and and_1 (and_1_out, ~bussplitter_1_d0, LD);  // And
  and and_2 (and_2_out, bussplitter_1_d0, LD);
  JK_FF_AS #(.Default(1)) jk_ff_as_1 (
    .Set(and_2_out), .J(EN), .C(C), .K(EN), .Clr(and_1_out), .Q(jk_ff_as_1_q), .nQ(jk_ff_as_1_nq));
  assign bussplitter_1_d0 = R ? jk_ff_as_1_q : 1'bz;  // Driver driver_1
  Multiplexer multiplexer_1 (.sel(DIR), .in_0(jk_ff_as_1_q), .in_1(jk_ff_as_1_nq), .out(multiplexer_1_out));
  and and_3 (and_3_out, EN, multiplexer_1_out);
  and and_4 (and_4_out, ~bussplitter_1_d1, LD);  // And
  and and_5 (and_5_out, bussplitter_1_d1, LD);
  JK_FF_AS jk_ff_as_2 (
    .Set(and_5_out), .J(and_3_out), .C(C), .K(and_3_out), .Clr(and_4_out), .Q(jk_ff_as_2_q),
    .nQ(jk_ff_as_2_nq));
  assign bussplitter_1_d1 = R ? jk_ff_as_2_q : 1'bz;  // Driver driver_2
  Multiplexer multiplexer_2 (.sel(DIR), .in_0(jk_ff_as_2_q), .in_1(jk_ff_as_2_nq), .out(multiplexer_2_out));
  and and_6 (and_6_out, and_3_out, multiplexer_2_out);
  and and_7 (and_7_out, ~bussplitter_1_d2, LD);  // And
  and and_8 (and_8_out, bussplitter_1_d2, LD);
  JK_FF_AS jk_ff_as_3 (
    .Set(and_8_out), .J(and_6_out), .C(C), .K(and_6_out), .Clr(and_7_out), .Q(jk_ff_as_3_q),
    .nQ(jk_ff_as_3_nq));
  assign bussplitter_1_d2 = R ? jk_ff_as_3_q : 1'bz;  // Driver driver_3
  Multiplexer multiplexer_3 (.sel(DIR), .in_0(jk_ff_as_3_q), .in_1(jk_ff_as_3_nq), .out(multiplexer_3_out));
  and and_9 (and_9_out, and_6_out, multiplexer_3_out);
  and and_10 (and_10_out, ~bussplitter_1_d3, LD);  // And
  and and_11 (and_11_out, bussplitter_1_d3, LD);
  JK_FF_AS jk_ff_as_4 (
    .Set(and_11_out), .J(and_9_out), .C(C), .K(and_9_out), .Clr(and_10_out), .Q(jk_ff_as_4_q),
    .nQ(jk_ff_as_4_nq));
  assign bussplitter_1_d3 = R ? jk_ff_as_4_q : 1'bz;  // Driver driver_4
  Multiplexer multiplexer_4 (.sel(DIR), .in_0(jk_ff_as_4_q), .in_1(jk_ff_as_4_nq), .out(multiplexer_4_out));
  and and_12 (and_12_out, and_9_out, multiplexer_4_out);
  and and_13 (and_13_out, ~bussplitter_1_d4, LD);  // And
  and and_14 (and_14_out, bussplitter_1_d4, LD);
  JK_FF_AS jk_ff_as_5 (
    .Set(and_14_out), .J(and_12_out), .C(C), .K(and_12_out), .Clr(and_13_out), .Q(jk_ff_as_5_q),
    .nQ(jk_ff_as_5_nq));
  assign bussplitter_1_d4 = R ? jk_ff_as_5_q : 1'bz;  // Driver driver_5
  Multiplexer multiplexer_5 (.sel(DIR), .in_0(jk_ff_as_5_q), .in_1(jk_ff_as_5_nq), .out(multiplexer_5_out));
  and and_15 (and_15_out, and_12_out, multiplexer_5_out);
  and and_16 (and_16_out, ~bussplitter_1_d5, LD);  // And
  and and_17 (and_17_out, bussplitter_1_d5, LD);
  JK_FF_AS jk_ff_as_6 (
    .Set(and_17_out), .J(and_15_out), .C(C), .K(and_15_out), .Clr(and_16_out), .Q(jk_ff_as_6_q),
    .nQ(jk_ff_as_6_nq));
  assign bussplitter_1_d5 = R ? jk_ff_as_6_q : 1'bz;  // Driver driver_6
  Multiplexer multiplexer_6 (.sel(DIR), .in_0(jk_ff_as_6_q), .in_1(jk_ff_as_6_nq), .out(multiplexer_6_out));
  and and_18 (and_18_out, and_15_out, multiplexer_6_out);
  and and_19 (and_19_out, ~bussplitter_1_d6, LD);  // And
  and and_20 (and_20_out, bussplitter_1_d6, LD);
  JK_FF_AS jk_ff_as_7 (
    .Set(and_20_out), .J(and_18_out), .C(C), .K(and_18_out), .Clr(and_19_out), .Q(jk_ff_as_7_q),
    .nQ(jk_ff_as_7_nq));
  assign bussplitter_1_d6 = R ? jk_ff_as_7_q : 1'bz;  // Driver driver_7
  Multiplexer multiplexer_7 (.sel(DIR), .in_0(jk_ff_as_7_q), .in_1(jk_ff_as_7_nq), .out(multiplexer_7_out));
  and and_21 (and_21_out, and_18_out, multiplexer_7_out);
  and and_22 (and_22_out, ~bussplitter_1_d7, LD);  // And
  and and_23 (and_23_out, bussplitter_1_d7, LD);
  JK_FF_AS jk_ff_as_8 (
    .Set(and_23_out), .J(and_21_out), .C(C), .K(and_21_out), .Clr(and_22_out), .Q(jk_ff_as_8_q));  // open: nQ
  assign bussplitter_1_d7 = R ? jk_ff_as_8_q : 1'bz;  // Driver driver_8
  nor nor_1 (INT, bussplitter_1_d7, bussplitter_1_d6, bussplitter_1_d5, bussplitter_1_d4, bussplitter_1_d3, bussplitter_1_d2, bussplitter_1_d1, bussplitter_1_d0);

  // Notes on the sheet:
  //   DIR: 0: Up
  //   1: Down
endmodule
