// Digital circuit TC_periph.dig as structural Verilog
// 4 8-bit timer counters
// Registers:
// TCxDAT - data in counter. R/W
// TCnCTRL - direction/enable signals for each timer.
// TCxINT - zero flags for each counter. These latch, and will remain set until cleared. R/W
// TCSZ - TC source/zero 	
// 	- bits 0-3 contain zero flags for each timer, which latch until reset. R/W(reset only)
// 	- bits 4-7 contain source selection for the clock: 0= timer, 1= counter
module TC_periph (
  input  [7:0] DAT,
  input  R,
  input  W,
  input  IOR,
  input  IOW,
  input  [15:0] ADD,
  input  C,
  input  [3:0] TCin
);

  wire ADD_TC0DAT_eq, ADD_TC1DAT_eq, ADD_TC2DAT_eq, ADD_TC3DAT_eq, ADD_TCCTRL_eq, ADD_TCSZ_eq, and_1_out,
       and_2_out, and_3_out, and_4_out, and_5_out, and_6_out, and_7_out, and_8_out, and_9_out, and_10_out,
       and_11_out, and_12_out, and_13_out, and_14_out, and_15_out, and_16_out, and_17_out, and_18_out,
       and_19_out, and_20_out, and_21_out, and_22_out, and_23_out, and_24_out, and_25_out, and_26_out,
       and_27_out, and_28_out, CSel0, CSel1, CSel2, CSel3, IOADD_TC0DAT_eq, IOADD_TC1DAT_eq, IOADD_TC2DAT_eq,
       IOADD_TC3DAT_eq, IOADD_TCCTRL_eq, IOADD_TCSZ_eq, multiplexer_1_out, multiplexer_2_out,
       multiplexer_3_out, multiplexer_4_out, or_1_out, or_2_out, or_3_out, or_4_out, or_5_out, or_6_out,
       or_7_out, or_8_out, or_9_out, or_10_out, or_11_out, or_12_out, TC0_DIR, TC0_EN, TC1_DIR, TC1_EN,
       TC2_DIR, TC2_EN, TC3_DIR, TC3_EN, Z0, Z1, Z2, Z3;
  wire [3:0] rs_ff_as_1_q, TCSZ_q;

  Comparator #(.Bits(16), .generic("this.Value = args.TCSZadd;")) ADD_TCSZ (
    .a(ADD), .b(16'h1), .eq(ADD_TCSZ_eq));  // open: gt, lt
  Comparator #(.Bits(16), .generic("this.Value = args.TCSZIOadd;")) IOADD_TCSZ (
    .a(ADD), .b(16'h1), .eq(IOADD_TCSZ_eq));  // open: gt, lt
  Comparator #(.Bits(16)) ADD_TCCTRL (.a(ADD), .b(16'h1), .eq(ADD_TCCTRL_eq));  // open: gt, lt
  Comparator #(.Bits(16)) IOADD_TCCTRL (.a(ADD), .b(16'h1), .eq(IOADD_TCCTRL_eq));  // open: gt, lt
  Comparator #(.Bits(16)) ADD_TC0DAT (.a(ADD), .b(16'h1), .eq(ADD_TC0DAT_eq));  // open: gt, lt
  Comparator #(.Bits(16)) IOADD_TC0DAT (.a(ADD), .b(16'h1), .eq(IOADD_TC0DAT_eq));  // open: gt, lt
  Comparator #(.Bits(16)) ADD_TC1DAT (.a(ADD), .b(16'h1), .eq(ADD_TC1DAT_eq));  // open: gt, lt
  Comparator #(.Bits(16)) IOADD_TC1DAT (.a(ADD), .b(16'h1), .eq(IOADD_TC1DAT_eq));  // open: gt, lt
  Comparator #(.Bits(16)) ADD_TC2DAT (.a(ADD), .b(16'h1), .eq(ADD_TC2DAT_eq));  // open: gt, lt
  Comparator #(.Bits(16)) IOADD_TC2DAT (.a(ADD), .b(16'h1), .eq(IOADD_TC2DAT_eq));  // open: gt, lt
  Comparator #(.Bits(16)) ADD_TC3DAT (.a(ADD), .b(16'h1), .eq(ADD_TC3DAT_eq));  // open: gt, lt
  Comparator #(.Bits(16)) IOADD_TC3DAT (.a(ADD), .b(16'h1), .eq(IOADD_TC3DAT_eq));  // open: gt, lt
  and and_1 (and_1_out, R, ADD_TCSZ_eq);
  and and_2 (and_2_out, IOR, IOADD_TCSZ_eq);
  and and_3 (and_3_out, ADD_TCSZ_eq, W);
  and and_4 (and_4_out, IOADD_TCSZ_eq, IOW);
  and and_5 (and_5_out, R, ADD_TCCTRL_eq);
  and and_6 (and_6_out, IOR, IOADD_TCCTRL_eq);
  and and_7 (and_7_out, ADD_TCCTRL_eq, W);
  and and_8 (and_8_out, IOADD_TCCTRL_eq, IOW);
  and and_9 (and_9_out, R, ADD_TC0DAT_eq);
  and and_10 (and_10_out, IOR, IOADD_TC0DAT_eq);
  and and_11 (and_11_out, ADD_TC0DAT_eq, W);
  and and_12 (and_12_out, IOADD_TC0DAT_eq, IOW);
  and and_13 (and_13_out, R, ADD_TC1DAT_eq);
  and and_14 (and_14_out, IOR, IOADD_TC1DAT_eq);
  and and_15 (and_15_out, ADD_TC1DAT_eq, W);
  and and_16 (and_16_out, IOADD_TC1DAT_eq, IOW);
  and and_17 (and_17_out, R, ADD_TC2DAT_eq);
  and and_18 (and_18_out, IOR, IOADD_TC2DAT_eq);
  and and_19 (and_19_out, ADD_TC2DAT_eq, W);
  and and_20 (and_20_out, IOADD_TC2DAT_eq, IOW);
  and and_21 (and_21_out, R, ADD_TC3DAT_eq);
  and and_22 (and_22_out, IOR, IOADD_TC3DAT_eq);
  and and_23 (and_23_out, ADD_TC3DAT_eq, W);
  and and_24 (and_24_out, IOADD_TC3DAT_eq, IOW);
  or or_1 (or_1_out, and_1_out, and_2_out);
  or or_2 (or_2_out, and_3_out, and_4_out);
  or or_3 (or_3_out, and_5_out, and_6_out);
  or or_4 (or_4_out, and_7_out, and_8_out);
  or or_5 (or_5_out, and_9_out, and_10_out);
  or or_6 (or_6_out, and_11_out, and_12_out);
  or or_7 (or_7_out, and_13_out, and_14_out);
  or or_8 (or_8_out, and_15_out, and_16_out);
  or or_9 (or_9_out, and_17_out, and_18_out);
  or or_10 (or_10_out, and_19_out, and_20_out);
  or or_11 (or_11_out, and_21_out, and_22_out);
  or or_12 (or_12_out, and_23_out, and_24_out);
  assign DAT = or_3_out ? {TC3_DIR, TC3_EN, TC2_DIR, TC2_EN, TC1_DIR, TC1_EN, TC0_DIR, TC0_EN} : 8'bz;  // Driver driver_1
  Register #(.Bits(8)) TC_ctrl (
    .D(DAT), .C(C), .en(or_4_out), .Q({TC3_DIR, TC3_EN, TC2_DIR, TC2_EN, TC1_DIR, TC1_EN, TC0_DIR, TC0_EN}));
  Multiplexer multiplexer_1 (.sel(CSel0), .in_0(C), .in_1(TCin[0]), .out(multiplexer_1_out));
  assign DAT = or_1_out ? {CSel3, CSel2, CSel1, CSel0, TCSZ_q} : 8'bz;  // Driver driver_2
  Multiplexer multiplexer_2 (.sel(CSel0), .in_0(C), .in_1(TCin[1]), .out(multiplexer_2_out));
  Multiplexer multiplexer_3 (.sel(CSel2), .in_0(C), .in_1(TCin[2]), .out(multiplexer_3_out));
  Multiplexer multiplexer_4 (.sel(CSel3), .in_0(C), .in_1(TCin[3]), .out(multiplexer_4_out));
  and and_25 (and_25_out, ~DAT[0], or_2_out);  // And
  and and_26 (and_26_out, ~DAT[1], or_2_out);  // And
  and and_27 (and_27_out, ~DAT[2], or_2_out);  // And
  and and_28 (and_28_out, ~DAT[3], or_2_out);  // And
  TC tc_1 (.DAT(DAT), .DIR(TC0_DIR), .R(or_5_out), .LD(or_6_out), .EN(TC0_EN), .C(multiplexer_1_out), .INT(Z0));
  TC tc_2 (.DAT(DAT), .DIR(TC1_DIR), .R(or_7_out), .LD(or_8_out), .EN(TC1_EN), .C(multiplexer_2_out), .INT(Z1));
  TC tc_3 (.DAT(DAT), .DIR(TC2_DIR), .R(or_9_out), .LD(or_10_out), .EN(TC2_EN), .C(multiplexer_3_out), .INT(Z2));
  TC tc_4 (.DAT(DAT), .DIR(TC3_DIR), .R(or_11_out), .LD(or_12_out), .EN(TC3_EN), .C(multiplexer_4_out), .INT(Z3));
  RS_FF_AS rs_ff_as_1 (.S(Z0), .R(and_25_out), .Q(rs_ff_as_1_q[0]));  // open: nQ
  RS_FF_AS rs_ff_as_2 (.S(Z1), .R(and_26_out), .Q(rs_ff_as_1_q[1]));  // open: nQ
  RS_FF_AS rs_ff_as_3 (.S(Z2), .R(and_27_out), .Q(rs_ff_as_1_q[2]));  // open: nQ
  RS_FF_AS rs_ff_as_4 (.S(Z3), .R(and_28_out), .Q(rs_ff_as_1_q[3]));  // open: nQ
  Register #(.Bits(8)) TCSZ (.D({DAT[7:4], rs_ff_as_1_q}), .C(C), .en(1'b1), .Q({CSel3, CSel2, CSel1, CSel0, TCSZ_q}));

  // Other names for the same wires on the sheet: ioread = IOR; iowrite = IOW; memread = R; memwrite = W;
  //   TC0_in = TCin[0]; TC1_in = TCin[1]; TC2_in = TCin[2]; TC3_in = TCin[3]
endmodule

/* Code that sets the parameters or builds the circuit:
zeroOffset:= 0;

TCSZIOadd:= 0x000C;
TCSZadd:= 0x0020;
TCCTRLadd:= 0x001F;
TCCTRLIOadd:= 0x000D;
TC0DATadd:=0x0021;
TC1DATadd:=0x0022;
TC2DATadd:=0x0023;
TC3DATadd:=0x0024;

TC0DATIOadd:=0x0008;
TC1DATIOadd:=0x0009;
TC2DATIOadd:=0x000A;
TC3DATIOadd:=0x000B;
*/
