// Digital circuit sysreg.dig as structural Verilog
module sysreg (
  input  [15:0] ADD,
  input  [7:0] DAT,
  input  R,
  input  W,
  input  C,
  output PWM0_EN,
  output PWM1_EN
);

  wire address_rw_1_r, address_rw_1_w;
  wire [7:2] SYSREG_q;

  Address_RW #(.generic("address := args.regAddress;")) address_rw_1 (
    .Ri(R), .Wi(W), .ADD(ADD), .R(address_rw_1_r), .W(address_rw_1_w));
  Register #(.Bits(8)) SYSREG (.D(DAT), .C(C), .en(address_rw_1_w), .Q({SYSREG_q, PWM1_EN, PWM0_EN}));
  assign DAT = address_rw_1_r ? {SYSREG_q, PWM1_EN, PWM0_EN} : 8'bz;  // Driver driver_1
  // Pins of 1 and 16 bits meet at ADD
endmodule

/* Code that sets the parameters or builds the circuit:
regAddress:= 0x0000;
*/
