// Digital circuit buckbjt.dig as structural Verilog
module buckbjt (
);

  wire _10V, capacitor_1_p1, capacitor_1_p2, DRV, NDRV, nmos_1_p1, nmos_1_p4, nmos_1_p5, PDRV;

  // AcVoltageSource #(.Amplitude(2)) acvoltagesource_1: pin names not known; wires that end beside it: 1'b0, 1'b0
  // DcVoltageSource dcvoltagesource_1: pin names not known; wires that end beside it: DRV, _10V, 1'b0
  // Resistor resistor_1: pin names not known; wires that end beside it: DRV
  // NpnBJT npnbjt_1: pin names not known
  // Resistor resistor_2: pin names not known; wires that end beside it: _10V, NDRV, NDRV, 1'b0
  // Resistor resistor_3: pin names not known; wires that end beside it: DRV
  // PnpBJT pnpbjt_1: pin names not known; wires that end beside it: PDRV
  // Resistor resistor_4: pin names not known; wires that end beside it: _10V, PDRV, 1'b0
  // Probe V_SUPPLY on nmos_1_p1
  // Probe V_SWITCH on nmos_1_p5
  // NMOS nmos_1: pin names not known; wires that end beside it: nmos_1_p1, _10V, NDRV, nmos_1_p4, nmos_1_p5
  // Inductor inductor_1: pin names not known; wires that end beside it: nmos_1_p4
  Diode #(.modelParams("{\"IS\":1e-14,\"N\":1,\"RS\":0,\"BV\":null,\"IBV\":0.001,\"CJO\":0,\"VJ\":0.7,\"M\":0.5,\"TT\":0,\"EG\":1.11,\"XTI\":3,\"KF\":0,\"AF\":1,\"FC\":0.5}")) diode_1 (.cathode(1'b0));  // open: anode
  // Probe V_OUT on capacitor_1_p2
  // Capacitor capacitor_1: pin names not known; wires that end beside it: capacitor_1_p1, capacitor_1_p2
  // Resistor resistor_5: pin names not known; wires that end beside it: capacitor_1_p1, 1'b0
endmodule
