// Digital circuit dcswitchlrc.dig as structural Verilog
module dcswitchlrc (
);

  wire analogcapacitor_1_p1, analogresistor_1_p2;

  // AnalogCapacitor #(.capacitance(0.0001)) analogcapacitor_1: pin names not known; wires that end beside it: analogcapacitor_1_p1, 1'b0
  // AnalogResistor #(.resistance(100)) analogresistor_1: pin names not known; wires that end beside it: analogcapacitor_1_p1, analogresistor_1_p2
  // AnalogInductor #(.inductance(0.1)) analoginductor_1: pin names not known; wires that end beside it: analogresistor_1_p2, 1'b0
  // SwitchDT switchdt_1: pin names not known; wires that end beside it: analogresistor_1_p2
  // DcVoltageSource dcvoltagesource_1: pin names not known; wires that end beside it: 1'b0
endmodule
