// Digital circuit lrctest.dig as structural Verilog
module lrctest (
);

  wire analogcapacitor_1_p1, analogcapacitor_1_p2, analogresistor_1_p2;

  // AnalogCapacitor analogcapacitor_1: pin names not known; wires that end beside it: analogcapacitor_1_p1, analogcapacitor_1_p2
  // AnalogResistor analogresistor_1: pin names not known; wires that end beside it: analogcapacitor_1_p1, analogresistor_1_p2
  // AnalogInductor analoginductor_1: pin names not known; wires that end beside it: analogresistor_1_p2, analogcapacitor_1_p2
  // AcVoltageSource acvoltagesource_1: pin names not known; wires that end beside it: analogcapacitor_1_p2
endmodule
