// Digital circuit step4-ram.dig as structural Verilog
module step4_ram (
  input  [7:0] Addr,
  input  [7:0] Din,
  input  WE,
  input  OE,
  input  CLK,
  output [7:0] Dout
);

  RAMDualPort #(.AddrBits(8), .Bits(8)) RAM (.A(Addr), .Din(Din), .str(WE), .C(CLK), .ld(OE), .D(Dout));
endmodule
