// Digital circuit step6-control-unit.dig as structural Verilog
module step6_control_unit (
  input  [1:0] Opcode,
  input  [1:0] Mode,
  output [1:0] ALU_Op,
  output RegWE,
  output RAM_WE,
  output [1:0] BusSel,
  output ALU_OE,
  output RAM_OE
);

  Decoder #(.Selector_Bits(2)) MODE_DEC (.out_0(ALU_OE), .out_1(RAM_WE), .out_2(RAM_OE));  // open: sel, out_3

  assign ALU_Op = Opcode;
  assign BusSel = Mode;
  assign RegWE = ALU_OE;
endmodule
