// Digital circuit ALU_checkpoint1.dig as structural Verilog
module ALU_checkpoint1 (
  input  [7:0] A,
  input  [7:0] B,
  input  Ci,
  input  [3:0] Select,
  output [7:0] Y,
  output Carry
);

  wire ADD_co, lsh_l_1_co, pulldown_2_out, rsh_a_1_co, rsh_l_1_co, sub_1_c_o;
  wire [7:0] ADD_out, and_1_out, lsh_l_1_out, neg_1_out, not_1_out, or_1_out, pulldown_1_out, rsh_a_1_out,
       rsh_l_1_out, sub_1_s, xor_1_out;
  wire [15:0] mul_1_mul;

  _8bit_adder ADD (.Ci(Ci), .IN1(A), .IN2(B), .OUT(ADD_out), .Co(ADD_co));
  lsh_l lsh_l_1 (.IN(A), .Ci(Ci), .OUT(lsh_l_1_out), .Co(lsh_l_1_co));
  rsh_l rsh_l_1 (.IN(A), .Ci(Ci), .OUT(rsh_l_1_out), .Co(rsh_l_1_co));
  rsh_a rsh_a_1 (.IN(A), .OUT(rsh_a_1_out), .Co(rsh_a_1_co));
  Sub #(.Bits(8)) sub_1 (.a(A), .b(B), .c_i(Ci), .s(sub_1_s), .c_o(sub_1_c_o));
  Mul #(.Signed("true"), .Bits(8)) mul_1 (.a(A), .b(B), .mul(mul_1_mul));
  Neg #(.Bits(8)) neg_1 (.in(A), .out(neg_1_out));
  assign and_1_out = A & B;  // And and_1, 8 bits wide
  assign or_1_out = A | B;  // Or or_1, 8 bits wide
  assign xor_1_out = A ^ B;  // XOr xor_1, 8 bits wide
  assign not_1_out = ~A;  // Not not_1, 8 bits wide
  PullDown #(.Bits(8)) pulldown_1 (.out(pulldown_1_out));
  PullDown pulldown_2 (.out(pulldown_2_out));
  Multiplexer #(.Selector_Bits(4), .Bits(8)) multiplexer_1 (
    .sel(Select), .in_0(ADD_out), .in_1(sub_1_s), .in_2(mul_1_mul[7:0]), .in_3(mul_1_mul[15:8]),
    .in_4(neg_1_out), .in_5(lsh_l_1_out), .in_6(rsh_l_1_out), .in_7(rsh_a_1_out), .in_8(and_1_out),
    .in_9(or_1_out), .in_10(xor_1_out), .in_11(not_1_out), .in_12(pulldown_1_out), .in_13(pulldown_1_out),
    .in_14(pulldown_1_out), .in_15(pulldown_1_out), .out(Y));
  Multiplexer #(.Selector_Bits(4)) multiplexer_2 (
    .sel(Select), .in_0(ADD_co), .in_1(sub_1_c_o), .in_2(pulldown_2_out), .in_3(pulldown_2_out),
    .in_4(pulldown_2_out), .in_5(lsh_l_1_co), .in_6(rsh_l_1_co), .in_7(rsh_a_1_co), .in_8(pulldown_2_out),
    .in_9(pulldown_2_out), .in_10(pulldown_2_out), .in_11(pulldown_2_out), .in_12(pulldown_2_out),
    .in_13(pulldown_2_out), .in_14(pulldown_2_out), .in_15(pulldown_2_out), .out(Carry));
endmodule
