// Digital circuit cpu_layout_CHECKPOINT4.dig as structural Verilog
module cpu_layout_CHECKPOINT4 (
  input  in_1,
  input  in_2,
  input  in_3,
  input  in_4,
  input  [3:0] in_5,
  input  [3:0] in_6,
  input  in_7,
  input  [4:0] in_8,
  input  in_9,
  input  in_10,
  input  in_11,
  input  in_12,
  input  in_13,
  input  [7:0] in_18,
  input  in_19,
  input  in_20,
  input  [11:0] in_21,
  input  in_22,
  input  in_23,
  input  in_24,
  input  in_25,
  input  in_28,
  input  clk,
  input  [7:0] DAT_2,
  input  [15:0] ADD_2,
  input  ext_data,
  input  ext_address,
  output [15:0] out_14,
  output out_15,
  output out_16,
  output out_17,
  output [15:0] ADD,
  output [7:0] DAT
);

  wire alu_complete_1_carry, alu_complete_1_neg, alu_complete_1_zero, and_1_out, and_2_out, and_3_out,
       and_4_out, and_5_out, comparator_1_eq, NOP_switch_q;
  wire [7:0] alu_complete_1_y, gpreg_addresses_1_rdest, gpreg_addresses_1_rsrc, multiplexer_2_out,
       multiplexer_3_out;
  wire [15:0] gpreg_addresses_1_adr, IR_q, pcfinal_1_pc, Program_d;

  assign DAT = ext_data ? DAT_2 : 8'bz;  // Driver driver_1
  assign ADD = ext_address ? ADD_2 : 16'bz;  // Driver driver_2
  pcfinal pcfinal_1 (.abs(in_3), .rel(in_4), .jump(ADD), .C(clk), .PC(pcfinal_1_pc));
  EEPROM #(.AddrBits(16), .isProgramMemory("true"), .Bits(16)) Program (
    .A(pcfinal_1_pc), .CS(1'b1), .WE(1'b0), .OE(1'b1), .D(Program_d));
  D_FF NOP_switch (.D(in_24), .C(clk), .Q(NOP_switch_q));  // open: nQ
  assign ADD = in_25 ? Program_d : 16'bz;  // Driver driver_3
  Register #(.Bits(16)) IR (.D(Program_d), .C(clk), .en(1'b1), .Q(IR_q));
  Multiplexer #(.Bits(16)) multiplexer_1 (.sel(NOP_switch_q), .in_0(IR_q), .in_1({16{1'b0}}), .out(out_14));
  GPReg_addresses gpreg_addresses_1 (
    .WD(DAT), .C(clk), .src(in_5), .dest(in_6), .WE(in_7), .Ra(in_23), .Rdest(gpreg_addresses_1_rdest),
    .Rsrc(gpreg_addresses_1_rsrc), .Adr(gpreg_addresses_1_adr));
  assign ADD = in_28 ? gpreg_addresses_1_adr : 16'bz;  // Driver driver_4
  assign DAT = in_11 ? gpreg_addresses_1_rsrc : 8'bz;  // Driver driver_5
  Multiplexer #(.Bits(8)) multiplexer_2 (
    .sel(in_12), .in_0(gpreg_addresses_1_rdest), .in_1(gpreg_addresses_1_rsrc), .out(multiplexer_2_out));
  Multiplexer #(.Bits(8)) multiplexer_3 (
    .sel(in_13), .in_0(gpreg_addresses_1_rsrc), .in_1(in_18), .out(multiplexer_3_out));
  ALU_complete alu_complete_1 (
    .A(multiplexer_2_out), .Op(in_8), .Y(alu_complete_1_y), .B(multiplexer_3_out), .Ci(out_15),
    .Carry(alu_complete_1_carry), .Zero(alu_complete_1_zero), .Neg(alu_complete_1_neg));
  status_reg status_reg_1 (
    .C(clk), .Zi(alu_complete_1_zero), .Ni(alu_complete_1_neg), .Ci(alu_complete_1_carry), .Zo(out_17),
    .No(out_16), .Co(out_15));
  assign DAT = in_9 ? alu_complete_1_y : 8'bz;  // Driver driver_6
  assign ADD = in_22 ? {{5{in_21[11]}}, in_21[10:0]} : 16'bz;  // Driver driver_7
  assign ADD = in_19 ? {{9{in_18[7]}}, in_18[6:0]} : 16'bz;  // Driver driver_8
  PullDown #(.Bits(16)) pulldown_1 (.out(ADD));
  and and_1 (and_1_out, ADD[14], ~ADD[15]);  // And
  Comparator comparator_1 (.a(ADD[15]), .b(1'b1), .eq(comparator_1_eq));  // open: gt, lt
  and and_2 (and_2_out, and_1_out, in_2);
  and and_3 (and_3_out, and_1_out, in_1);
  and and_4 (and_4_out, comparator_1_eq, clk, in_2);
  and and_5 (and_5_out, comparator_1_eq, in_1);
  RAMSinglePort #(.AddrBits(14), .Bits(8)) RAM (.A(ADD[13:0]), .str(and_2_out), .C(clk), .ld(and_3_out), .D(DAT));
  EEPROM #(.AddrBits(15), .Bits(8)) FLASH (
    .A(ADD[14:0]), .CS(comparator_1_eq), .WE(and_4_out), .OE(and_5_out), .D(DAT));
  assign DAT = in_20 ? in_18 : 8'bz;  // Driver driver_9
  PullDown #(.Bits(8)) pulldown_2 (.out(DAT));

  // Other names for the same wires on the sheet: ALU_add = in_10; ALU_ADR = in_12; ALU_BRI = in_13; ALU_data = in_9;
  //   C = clk; Co = out_15; Imm_add = in_19; Imm_data = in_20; ImmVal[7:0] = in_18; INSTR[15:0] = out_14;
  //   j_abs = in_3; j_rel = in_4; N = out_16; NXT_add = in_25; OP_ALU[4:0] = in_8; R_add = in_1; Ra = in_23;
  //   RA_add = in_28; reg_dest[3:0] = in_6; reg_src[3:0] = in_5; rjmp[11:0] = in_21; rjmp_add = in_22; SKIP = in_24;
  //   SRC_data = in_11; W_add = in_2; W_reg = in_7; Z = out_17

  // Notes on the sheet:
  //   Control Circuit
  //   contents of Program (hex, n*v repeats v):
  //   0,a130,8000,a140,8001,a150,8002,a160,8003,c73,174,d0b4,5f6f,174
  //   ,d0b1,f000,a,c86,284,138,b106,4000,b103,4001
  //   contents of FLASH (hex, n*v repeats v):
  //   11,5,1,1,12*0,a1,60,1262*0,f,9962*0,2b,6164*0,f1,3f,2560*0,fa
  //   ,8703*0,3,2
endmodule
