// Digital circuit cpu_layout_final.dig as structural Verilog
module cpu_layout_final (
  input  clk,
  input  [7:0] DAT,
  input  [15:0] ADD,
  output [15:0] ADD_2,
  output [7:0] DAT_2
);

  wire ALU_ADR, ALU_BRI, alu_complete_1_carry, alu_complete_1_neg, alu_complete_1_zero, ALU_data, and_1_out,
       and_2_out, and_3_out, and_4_out, and_5_out, Co, comparator_1_eq, Imm_add, Imm_data, INSTR, j_abs,
       j_rel, N, NOP_switch_q, NXT_add, R_add, Ra, RA_add, reg_dest, reg_src, rjmp_add, SKIP, SRC_data,
       W_add, W_reg, Z;
  wire [4:0] OP_ALU;
  wire [7:0] alu_complete_1_y, gpreg_addresses_1_p7, gpreg_addresses_1_p8, gpreg_addresses_1_p9, ImmVal,
       multiplexer_2_out, multiplexer_3_out;
  wire [11:0] rjmp;
  wire [15:0] IR_q, pcfinal_1_pc, Program_d;

  pcfinal pcfinal_1 (.abs(j_abs), .rel(j_rel), .jump(ADD), .C(clk), .PC(pcfinal_1_pc));
  EEPROM #(.AddrBits(16), .isProgramMemory("true"), .Bits(16)) Program (
    .A(pcfinal_1_pc), .CS(1'b1), .WE(1'b0), .OE(1'b1), .D(Program_d));
  D_FF NOP_switch (.D(SKIP), .C(clk), .Q(NOP_switch_q));  // open: nQ
  assign ADD[7:0] = NXT_add ? Program_d[7:0] : 8'bz;  // Driver driver_1
  Register #(.Bits(16)) IR (.D(Program_d), .C(clk), .en(1'b1), .Q(IR_q));
  Multiplexer multiplexer_1 (.sel(NOP_switch_q), .in_0(IR_q[0]), .in_1(1'b0), .out(INSTR));
  // GPReg_addresses gpreg_addresses_1: pin names not known; wires that end beside it: DAT, clk, reg_src, reg_dest, W_reg, Ra, gpreg_addresses_1_p7, gpreg_addresses_1_p8, gpreg_addresses_1_p9
  assign ADD[7:0] = RA_add ? gpreg_addresses_1_p9 : 8'bz;  // Driver driver_2
  assign DAT = SRC_data ? gpreg_addresses_1_p8 : 8'bz;  // Driver driver_3
  Multiplexer #(.Bits(8)) multiplexer_2 (
    .sel(ALU_ADR), .in_0(gpreg_addresses_1_p7), .in_1(gpreg_addresses_1_p8), .out(multiplexer_2_out));
  Multiplexer #(.Bits(8)) multiplexer_3 (
    .sel(ALU_BRI), .in_0(gpreg_addresses_1_p8), .in_1(ImmVal), .out(multiplexer_3_out));
  ALU_complete alu_complete_1 (
    .A(multiplexer_2_out), .Op(OP_ALU), .Y(alu_complete_1_y), .B(multiplexer_3_out), .Ci(Co),
    .Carry(alu_complete_1_carry), .Zero(alu_complete_1_zero), .Neg(alu_complete_1_neg));
  status_reg status_reg_1 (
    .Zi(alu_complete_1_zero), .Ni(alu_complete_1_neg), .Ci(alu_complete_1_carry), .Zo(Z), .No(N), .Co(Co));  // open: C
  assign DAT = ALU_data ? alu_complete_1_y : 8'bz;  // Driver driver_4
  Driver #(.Bits(16)) driver_5 (.in({{5{rjmp[11]}}, rjmp[10:0]}), .en(rjmp_add));  // open: out
  Driver #(.Bits(16)) driver_6 (.in({{9{ImmVal[7]}}, ImmVal[6:0]}), .en(Imm_add));  // open: out
  and and_1 (and_1_out, ADD[14], ~ADD[15]);  // And
  Comparator comparator_1 (.a(ADD[15]), .b(1'b1), .eq(comparator_1_eq));  // open: gt, lt
  and and_2 (and_2_out, and_1_out, W_add);
  and and_3 (and_3_out, and_1_out, R_add);
  and and_4 (and_4_out, comparator_1_eq, clk, W_add);
  and and_5 (and_5_out, comparator_1_eq, R_add);
  RAMSinglePort #(.AddrBits(14), .Bits(8)) RAM (.A(ADD[13:0]), .str(and_2_out), .C(clk), .ld(and_3_out), .D(DAT));
  EEPROM #(.AddrBits(15), .Bits(8)) FLASH (
    .A(ADD[14:0]), .CS(comparator_1_eq), .WE(and_4_out), .OE(and_5_out), .D(DAT));
  Driver #(.Bits(8)) driver_7 (.in(ImmVal), .en(Imm_data));  // open: out
  // Pins of 8 and 16 bits meet at Program_d
  // Pins of 1 and 16 bits meet at IR_q
  // Pins of 8 and 16 bits meet at ADD
  // Pins of 1 and 16 bits meet at {16{1'b0}}

  assign ADD_2 = ADD;
  assign DAT_2 = DAT;

  // Other names for the same wires on the sheet: C = clk

  // Notes on the sheet:
  //   contents of Program (hex, n*v repeats v):
  //   e001a130,f000,a140,f001,a150,f002,a160,f04b,c73,174,d0b4,4061
  //   ,174,d0b1,f000,b,c86,284,138,b160,f002,b130,f003,4073*0,f000,40
  //   Control Circuit
  //   contents of FLASH (hex, n*v repeats v):
  //   11,5,1278*0,f
endmodule
