// Digital circuit cpu_layout_start.dig as structural Verilog
module cpu_layout_start (
  input  clk,
  input  [7:0] DAT,
  input  [15:0] ADD,
  input  in_6,
  input  in_7,
  input  ext_data,
  input  ext_address,
  output [15:0] ADD_2,
  output [7:0] DAT_2
);

  wire and_1_out, and_2_out, and_3_out, and_4_out, and_5_out, comparator_1_eq;

  assign DAT_2 = ext_data ? DAT : 8'bz;  // Driver driver_1
  assign ADD_2 = ext_address ? ADD : 16'bz;  // Driver driver_2
  pcfinal pcfinal_1 ();  // open: abs, rel, jump, C, PC
  EEPROM #(.AddrBits(16), .isProgramMemory("true"), .Bits(16)) Program (.CS(1'b1), .WE(1'b0), .OE(1'b1));  // open: A, D
  Register #(.Bits(16)) IR (.en(1'b1));  // open: D, C, Q
  // GPReg gpreg_1: pin names not known; wires that end beside it: clk
  ALU_complete alu_complete_1 ();  // open: A, Op, Y, B, Ci, Carry, Zero, Neg
  // status_reg status_reg_1: pin names not known; wires that end beside it: clk
  and and_1 (and_1_out, ADD_2[14], ~ADD_2[15]);  // And
  Comparator comparator_1 (.a(ADD_2[15]), .b(1'b1), .eq(comparator_1_eq));  // open: gt, lt
  and and_2 (and_2_out, and_1_out, in_7);
  and and_3 (and_3_out, and_1_out, in_6);
  and and_4 (and_4_out, comparator_1_eq, clk, in_7);
  and and_5 (and_5_out, comparator_1_eq, in_6);
  RAMSinglePort #(.AddrBits(14), .Bits(8)) RAM (.A(ADD_2[13:0]), .str(and_2_out), .C(clk), .ld(and_3_out), .D(DAT_2));
  EEPROM #(.AddrBits(15), .Bits(8)) FLASH (
    .A(ADD_2[14:0]), .CS(comparator_1_eq), .WE(and_4_out), .OE(and_5_out), .D(DAT_2));

  // Other names for the same wires on the sheet: C = clk; mem2data = in_6; str_mem = in_7

  // Notes on the sheet:
  //   Control Circuit
  //   contents of Program (hex, n*v repeats v):
  //   e001a130,f000,a140,f001,a150,f002,a160,f04b,c73,174,d0b4,4061
  //   ,174,d0b1,f000,b,c86,284,138,b160,f002,b130,f003,4073*0,f000,40
  //   contents of FLASH (hex, n*v repeats v):
  //   11,5,1278*0,f
endmodule
