// Digital circuit flag_check.dig as structural Verilog
module flag_check (
  input  Co,
  input  N,
  input  Z,
  input  [2:0] s,
  output br
);

  wire not_1_out, or_1_out;

  or or_1 (or_1_out, N, Z);
  not not_1 (not_1_out, N);
  Multiplexer #(.Selector_Bits(3)) multiplexer_1 (
    .sel(s), .in_0(Co), .in_1(N), .in_2(Z), .in_3(or_1_out), .in_4(not_1_out), .in_5(1'b0), .in_6(1'b0),
    .in_7(1'b0), .out(br));
endmodule

/* Test case:
Co N Z s  br

0 x x 0  0
1 x x 0  1
x 0 x 1  0
x 1 x 1  1
x x 0 2  0
x x 1 2  1
x 0 0 3  0
x 0 1 3  1
x 1 0 3  1
x 1 1 3  1

x 0 0 4  1
x 0 1 4  1
x 1 0 4  0
x 1 1 4  0
*/
