// Digital circuit intro.dig as structural Verilog
module intro (
  input  A3,
  input  B3,
  input  A2,
  input  B2,
  input  A1,
  input  B1,
  input  A0,
  input  B0,
  input  [3:0] A,
  input  [3:0] B,
  input  [15:0] BUS_IN,
  input  [7:0] SPLIT_IN,
  output C3,
  output C2,
  output C1,
  output C0,
  output [3:0] C,
  output [15:0] BUS_OUT,
  output [7:0] SPLIT_OUT
);

  and and_1 (C3, A3, B3);
  and and_2 (C2, A2, B2);
  and and_3 (C1, A1, B1);
  and and_4 (C0, A0, B0);
  assign C = A & B;  // And and_5, 4 bits wide
  // Pins of 1 and 16 bits meet at BUS_IN

  assign BUS_OUT = BUS_IN;
  assign SPLIT_OUT = SPLIT_IN;

  // Notes on the sheet:
  //   A3: default 1
  //   B3: default 1
  //   A2: default 1
  //   B2: default 1
  //   B0: default 1
  //   A: default 12
  //   B: default 13
  //   SPLIT_IN: default 3
endmodule
