// Digital circuit memory_scale_up.dig as structural Verilog
module memory_scale_up (
  input  [7:0] D,
  input  [3:0] A,
  input  R,
  input  W,
  input  C,
  output [7:0] D_O
);

  wire and_1_out, and_2_out, and_3_out, or_1_out, or_2_out, or_3_out;

  or or_1 (or_1_out, W, A[3], ~A[2]);  // Or
  and and_1 (and_1_out, R, ~A[3], A[2]);  // And
  or or_2 (or_2_out, W, A[2], A[3]);
  and and_2 (and_2_out, R, ~A[2], ~A[3]);  // And
  or or_3 (or_3_out, W, ~A[3]);  // Or
  and and_3 (and_3_out, R, A[3]);
  _8x8bitreg_block Address_8_15__red (.D(D), .A(A[2:0]), .W(or_3_out), .C(C), .R(and_3_out), .D_O(D_O));
  _4x8bitreg_block Address_4_7__blue (.D(D), .A(A[1:0]), .W(or_1_out), .C(C), .R(and_1_out), .D_O(D_O));
  _4x8bitreg_block Address_0_3__green (.D(D), .A(A[1:0]), .W(or_2_out), .C(C), .R(and_2_out), .D_O(D_O));

  // Notes on the sheet:
  //   W: default 1
endmodule

/* Test case:
C A D !W R  D_O

loop (B, 16)
  

    0 (B) 0 0 0   0
    C (B) 0 0 0   0
    C (B) X 1 1   0
    C (B) X 1 1   0
    C (B) 0 0 1   0

    loop (E, 256)
      C (B) (E)  0 0  0
      C (B)  X   1 1 (E)
    end loop
end loop
*/
