// Digital circuit single_8bit_register.dig as structural Verilog
// Single 8-bit register. D_O port has an internal buffer so should be connectable to the input bus.
module single_8bit_register (
  input  [7:0] D,
  input  W,
  input  R,
  input  C,
  output [7:0] D_O
);

  wire driver_1_out, not_1_out;
  wire [0:0] d_ms_6_p3, d_ms_7_p3, d_ms_8_p3;
  wire [4:0] d_ms_1_p3;

  assign driver_1_out = not_1_out ? C : 1'bz;  // Driver driver_1
  not not_1 (not_1_out, W);
  // D_MS d_ms_1: pin names not known; wires that end beside it: D[7], driver_1_out, d_ms_1_p3[4]
  // D_MS d_ms_2: pin names not known; wires that end beside it: D[6], driver_1_out, d_ms_1_p3[3]
  // D_MS d_ms_3: pin names not known; wires that end beside it: D[5], driver_1_out, d_ms_1_p3[2]
  // D_MS d_ms_4: pin names not known; wires that end beside it: D[4], driver_1_out, d_ms_1_p3[1]
  // D_MS d_ms_5: pin names not known; wires that end beside it: D[3], driver_1_out, d_ms_1_p3[0]
  // D_MS d_ms_6: pin names not known; wires that end beside it: D[2], driver_1_out, d_ms_6_p3[0]
  // D_MS d_ms_7: pin names not known; wires that end beside it: D[1], driver_1_out, d_ms_7_p3[0]
  // D_MS d_ms_8: pin names not known; wires that end beside it: D[0], driver_1_out, d_ms_8_p3[0]
  PullDown pulldown_1 (.out(driver_1_out));
  assign D_O = R ? {d_ms_1_p3, d_ms_6_p3[0], d_ms_7_p3[0], d_ms_8_p3[0]} : 8'bz;  // Driver driver_2
  PullDown #(.Bits(8)) pulldown_2 (.out(D_O));

  // Notes on the sheet:
  //   W: 0 = Write, default 1
  //   R: 1 = Read
endmodule

/* Test case:
C D !W R  D_O


0 0  0 0   0
C 0  0 0   0
C X  1 1   0
C X  1 1   0
C 0  0 1   0

loop (A, 256)
  C (A)  0 0   0
  C  X   1 1  (A)
end loop
*/
