// Digital circuit pccheckpoint1.dig as structural Verilog
// Program Counter for 10-bit program memory
// Incorporates a program counter register and branching logic.
// Inputs:
// C	Clock
// R	Reset register to 0
// jump[10]	Increment or absolute address to branch to
// rel	PC is incremented by jump if rel is high
// abs	PC is loaded with jump if abs is high (if rel and abs are high, abs wins)
// Outputs:
// PC[10]	Current instruction address
// NEXT[10]	PC + 1 (next address if no branch)
module pccheckpoint1 (
  input  C,
  output [15:0] PC
);

  wire [15:0] ADD_1_s;

  Register #(.Bits(16), .isProgramCounter("true")) u_PC (.D(ADD_1_s), .C(C), .en(1'b1), .Q(PC));
  Add #(.Bits(16)) ADD_1 (.a(PC), .b(16'h1), .c_i(1'b0), .s(ADD_1_s));  // open: c_o
endmodule
