// Digital circuit program_navigation_checkpoint1.dig as structural Verilog
module program_navigation_checkpoint1 (
  input  clk,
  output [15:0] out_2
);

  wire [15:0] pccheckpoint1_1_pc, PROGRAM_d;

  pccheckpoint1 pccheckpoint1_1 (.C(clk), .PC(pccheckpoint1_1_pc));
  EEPROM #(.AddrBits(16), .Bits(16)) PROGRAM (.A(pccheckpoint1_1_pc), .CS(1'b1), .WE(1'b0), .OE(1'b1), .D(PROGRAM_d));
  Register #(.Bits(16)) IR (.D(PROGRAM_d), .C(clk), .en(1'b1), .Q(out_2));

  // Other names for the same wires on the sheet: C = clk

  // Notes on the sheet:
  //   contents of PROGRAM (hex, n*v repeats v):
  //   1,4,6,6,3,2,1a,0,2c,25,38,2e5,2e,5,ee,54565,15a,15c,2b,5,4,95c
  //   ,2b,1c,15a53245,20b,0,0,6,0,6,14*0,42
endmodule
