// Digital circuit status_reg.dig as structural Verilog
module status_reg (
  input  C,
  input  Zi,
  input  Ni,
  input  Ci,
  output Zo,
  output No,
  output Co
);

  wire pullup_1_out;
  wire [4:0] pulldown_1_out;
  wire [7:3] register_1_q;

  PullDown #(.Bits(5)) pulldown_1 (.out(pulldown_1_out));
  PullUp pullup_1 (.out(pullup_1_out));
  Register #(.Bits(8)) register_1 (
    .D({pulldown_1_out, Zi, Ni, Ci}), .C(C), .en(pullup_1_out), .Q({register_1_q, Zo, No, Co}));
  PullDown #(.Bits(5)) pulldown_2 (.out(register_1_q));
endmodule
