// Digital circuit zero_check.dig as structural Verilog
module zero_check (
  input  [7:0] IN,
  output ZERO
);

  nor nor_1 (ZERO, IN[0], IN[1], IN[2], IN[3], IN[4], IN[5], IN[6], IN[7]);
endmodule

/* Test case:
IN ZERO
0  1

loop (A,255)
  (A+1) 0
end loop
*/
