// Digital circuit step-2-alu-goal.dig as structural Verilog
module step_2_alu_goal (
  input  [7:0] A,
  input  [7:0] B,
  input  [1:0] Op,
  output [7:0] Y,
  output Cout
);

  wire [7:0] ADD_s, AND_out, OR_out, SUB_s;

  Add #(.Bits(8)) ADD (.a(A), .b(B), .c_i(1'b0), .s(ADD_s), .c_o(Cout));
  Sub #(.Bits(8)) SUB (.a(A), .b(B), .c_i(1'b0), .s(SUB_s));  // open: c_o
  assign AND_out = A & B;  // And AND, 8 bits wide
  assign OR_out = A | B;  // Or OR, 8 bits wide
  Multiplexer #(.Selector_Bits(2), .Bits(8)) MUX (
    .sel(Op), .in_0(ADD_s), .in_1(SUB_s), .in_2(AND_out), .in_3(OR_out), .out(Y));
endmodule
