// Digital circuit step-4-ram-goal.dig as structural Verilog
module step_4_ram_goal (
  input  [7:0] Addr,
  input  [7:0] Din,
  input  WE,
  input  [7:0] OE,
  input  CLK,
  output [7:0] Dout
);

  RAMDualPort #(.AddrBits(8), .Bits(8)) RAM (.A(Addr), .Din(Din), .str(WE), .C(CLK), .D(OE));  // open: ld
  // Pins of 1 and 8 bits meet at OE

  assign Dout = OE;
endmodule
