// Digital circuit step-5-data-bus-goal.dig as structural Verilog
module step_5_data_bus_goal (
  input  [7:0] ALU_out,
  input  [7:0] RAM_out,
  input  [7:0] IMM,
  input  [1:0] BusSel,
  output [7:0] BUS
);

  Multiplexer #(.Selector_Bits(2), .Bits(8)) BUS_MUX (
    .sel(BusSel), .in_0(ALU_out), .in_1(RAM_out), .in_2(IMM), .in_3({8{1'b0}}), .out(BUS));
endmodule
