// Digital circuit step-7-flags-goal.dig as structural Verilog
module step_7_flags_goal (
  input  [7:0] ALU_Result,
  input  Carry_in,
  input  Flag_WE,
  input  CLK,
  output C_flag,
  output Z_flag
);

  wire ZERO_DET_eq;

  Comparator #(.Bits(8)) ZERO_DET (.a(ALU_Result), .b({8{1'b0}}), .eq(ZERO_DET_eq));  // open: gt, lt
  Register #(.Bits(1)) ZF (.D(ZERO_DET_eq), .C(CLK), .en(Flag_WE), .Q(Z_flag));
  Register #(.Bits(1)) CF (.D(Carry_in), .C(CLK), .en(Flag_WE), .Q(C_flag));
endmodule
