// Digital circuit gated-sr-goal.dig as structural Verilog
module gated_sr_goal (
  input  S,
  input  R,
  input  E,
  output Q,
  output nQ
);

  wire A1_out, A2_out;

  nand A1 (A1_out, S, E);
  nand A2 (A2_out, E, R);
  nand G1 (Q, A1_out, nQ);
  nand G2 (nQ, Q, A2_out);
endmodule
